// Logisim project Projet_Final.circ as structural Verilog: 46 circuits, main circuit Montre_main
module Montre_main (
  output Musique,
  output Terre
);

  wire Alarm_1_beep_beep, B_action_out, B_mode_out, Debouncer_1_debounced_button,
       Debouncer_2_debounced_button, Demux_Manager_1_led_alarm, Demux_Manager_1_led_fuseau_horaire,
       Demux_Manager_1_led_horloge, Demux_Manager_1_led_stopwatch, Demux_Manager_1_led_timer,
       Demux_Manager_1_stop_musique, DipSwitch_1_sw1, DipSwitch_1_sw4, DipSwitch_1_sw5, DipSwitch_1_sw6,
       DipSwitch_1_sw7, DipSwitch_1_sw8, DipSwitch_1_sw9, DipSwitch_1_sw10, not_1_out, or_1_out, or_2_out,
       Timer_1_zero;
  wire [1:0] Demux_Manager_1_stopwatch;
  wire [2:0] Demux_Manager_1_fuseau_horaire, Select_mode_1_mode;
  wire [7:0] Fuseau_horaire_1_heure_10_affichage, Fuseau_horaire_1_heure_affichage,
       Fuseau_horaire_1_minute_10_affichage, Fuseau_horaire_1_minute_affichage,
       Fuseau_horaire_1_seconde_10_affichage, Fuseau_horaire_1_seconde_affichage;
  wire [8:0] Demux_Manager_1_horloge, Demux_Manager_1_timer;
  wire [9:0] Demux_Manager_1_alarm;
  wire [29:0] Alarm_1_alarm_out, Horloge_2_horloge_out, Mux_Manager_1_mux_out, Stopwatch_1_stopwatch_out,
       Timer_1_timer_out;

  Button B_mode (.out(B_mode_out));
  Button B_action (.out(B_action_out));
  Debouncer Debouncer_1 (.Button(B_mode_out), .Debounced_button(Debouncer_1_debounced_button));
  Debouncer Debouncer_2 (.Button(B_action_out), .Debounced_button(Debouncer_2_debounced_button));
  not not_1 (not_1_out, DipSwitch_1_sw1);
  LED Board_Activated (.in(DipSwitch_1_sw1));
  DipSwitch #(.number(10)) DipSwitch_1 (
    .sw1(DipSwitch_1_sw1), .sw4(DipSwitch_1_sw4), .sw5(DipSwitch_1_sw5), .sw6(DipSwitch_1_sw6),
    .sw7(DipSwitch_1_sw7), .sw8(DipSwitch_1_sw8), .sw9(DipSwitch_1_sw9), .sw10(DipSwitch_1_sw10));  // open: sw2, sw3
  Select_mode Select_mode_1 (.B_mode(Debouncer_1_debounced_button), .Reset(not_1_out), .Mode(Select_mode_1_mode));
  _7_Segment_Display L_7_Segment_Display_4 (
    .g(Fuseau_horaire_1_heure_10_affichage[6]), .f(Fuseau_horaire_1_heure_10_affichage[5]),
    .a(Fuseau_horaire_1_heure_10_affichage[0]), .b(Fuseau_horaire_1_heure_10_affichage[1]),
    .e(Fuseau_horaire_1_heure_10_affichage[4]), .d(Fuseau_horaire_1_heure_10_affichage[3]),
    .c(Fuseau_horaire_1_heure_10_affichage[2]), .dp(Fuseau_horaire_1_heure_10_affichage[7]));
  _7_Segment_Display L_7_Segment_Display_5 (
    .g(Fuseau_horaire_1_heure_affichage[6]), .f(Fuseau_horaire_1_heure_affichage[5]),
    .a(Fuseau_horaire_1_heure_affichage[0]), .b(Fuseau_horaire_1_heure_affichage[1]),
    .e(Fuseau_horaire_1_heure_affichage[4]), .d(Fuseau_horaire_1_heure_affichage[3]),
    .c(Fuseau_horaire_1_heure_affichage[2]), .dp(Fuseau_horaire_1_heure_affichage[7]));
  Demux_Manager Demux_Manager_1 (
    .Reset_All(not_1_out), .s1_in(DipSwitch_1_sw5), .Bouton_action(Debouncer_2_debounced_button),
    .s2_in(DipSwitch_1_sw6), .m1_in(DipSwitch_1_sw7), .m2_in(DipSwitch_1_sw8), .h1_in(DipSwitch_1_sw9),
    .Stand_by_Alarm_in(DipSwitch_1_sw4), .h2_in(DipSwitch_1_sw10), .Mode(Select_mode_1_mode),
    .Horloge(Demux_Manager_1_horloge), .LED_Horloge(Demux_Manager_1_led_horloge),
    .Alarm(Demux_Manager_1_alarm), .LED_Alarm(Demux_Manager_1_led_alarm),
    .LED_Stopwatch(Demux_Manager_1_led_stopwatch), .Stopwatch(Demux_Manager_1_stopwatch),
    .Timer(Demux_Manager_1_timer), .LED_Timer(Demux_Manager_1_led_timer),
    .Fuseau_horaire(Demux_Manager_1_fuseau_horaire), .LED_Fuseau_horaire(Demux_Manager_1_led_fuseau_horaire),
    .Musique_on(or_2_out), .Stop_musique(Demux_Manager_1_stop_musique));
  LED ALARMEE (.in(Demux_Manager_1_led_alarm));
  LED LED_Stopwatch (.in(Demux_Manager_1_led_stopwatch));
  LED LED_Timer (.in(Demux_Manager_1_led_timer));
  LED fuseau_horaireee (.in(Demux_Manager_1_led_fuseau_horaire));
  _7_Segment_Display L_7_Segment_Display_6 (
    .g(Fuseau_horaire_1_minute_10_affichage[6]), .f(Fuseau_horaire_1_minute_10_affichage[5]),
    .a(Fuseau_horaire_1_minute_10_affichage[0]), .b(Fuseau_horaire_1_minute_10_affichage[1]),
    .e(Fuseau_horaire_1_minute_10_affichage[4]), .d(Fuseau_horaire_1_minute_10_affichage[3]),
    .c(Fuseau_horaire_1_minute_10_affichage[2]), .dp(Fuseau_horaire_1_minute_10_affichage[7]));
  LED LED_Horloge (.in(Demux_Manager_1_led_horloge));
  or or_1 (or_1_out, Demux_Manager_1_stop_musique, not_1_out);
  Horloge Horloge_2 (.Horloge_in(Demux_Manager_1_horloge), .Horloge_out(Horloge_2_horloge_out));
  _7_Segment_Display L_7_Segment_Display_1 (
    .g(Fuseau_horaire_1_minute_affichage[6]), .f(Fuseau_horaire_1_minute_affichage[5]),
    .a(Fuseau_horaire_1_minute_affichage[0]), .b(Fuseau_horaire_1_minute_affichage[1]),
    .e(Fuseau_horaire_1_minute_affichage[4]), .d(Fuseau_horaire_1_minute_affichage[3]),
    .c(Fuseau_horaire_1_minute_affichage[2]), .dp(Fuseau_horaire_1_minute_affichage[7]));
  _7_Segment_Display L_7_Segment_Display_2 (
    .g(Fuseau_horaire_1_seconde_10_affichage[6]), .f(Fuseau_horaire_1_seconde_10_affichage[5]),
    .a(Fuseau_horaire_1_seconde_10_affichage[0]), .b(Fuseau_horaire_1_seconde_10_affichage[1]),
    .e(Fuseau_horaire_1_seconde_10_affichage[4]), .d(Fuseau_horaire_1_seconde_10_affichage[3]),
    .c(Fuseau_horaire_1_seconde_10_affichage[2]), .dp(Fuseau_horaire_1_seconde_10_affichage[7]));
  Alarm Alarm_1 (
    .Alarm_in(Demux_Manager_1_alarm), .Horloge_in(Horloge_2_horloge_out), .Alarm_out(Alarm_1_alarm_out),
    .BEEP_BEEP(Alarm_1_beep_beep));
  Stopwatch Stopwatch_1 (.Stopwatch_in(Demux_Manager_1_stopwatch), .Stopwatch_out(Stopwatch_1_stopwatch_out));
  Timer Timer_1 (.Timer_in(Demux_Manager_1_timer), .Timer_out(Timer_1_timer_out), .Zero(Timer_1_zero));
  or or_2 (or_2_out, Alarm_1_beep_beep, Timer_1_zero);
  _7_Segment_Display L_7_Segment_Display_3 (
    .g(Fuseau_horaire_1_seconde_affichage[6]), .f(Fuseau_horaire_1_seconde_affichage[5]),
    .a(Fuseau_horaire_1_seconde_affichage[0]), .b(Fuseau_horaire_1_seconde_affichage[1]),
    .e(Fuseau_horaire_1_seconde_affichage[4]), .d(Fuseau_horaire_1_seconde_affichage[3]),
    .c(Fuseau_horaire_1_seconde_affichage[2]), .dp(Fuseau_horaire_1_seconde_affichage[7]));
  Mux_Manager Mux_Manager_1 (
    .Mode(Select_mode_1_mode), .Horloge(Horloge_2_horloge_out), .Alarm(Alarm_1_alarm_out),
    .Stopwatch(Stopwatch_1_stopwatch_out), .Timer(Timer_1_timer_out), .Mux_out(Mux_Manager_1_mux_out));
  Harry_Potter Harry_Potter_1 (.BEEP_BEEP(or_2_out), .Stop(or_1_out), .Musique(Musique), .Terre(Terre));
  Fuseau_horaire Fuseau_horaire_1 (
    .Heure(Mux_Manager_1_mux_out), .Fuseau_horaire_in(Demux_Manager_1_fuseau_horaire),
    .Seconde_affichage(Fuseau_horaire_1_seconde_affichage),
    .Seconde_10_affichage(Fuseau_horaire_1_seconde_10_affichage),
    .Minute_affichage(Fuseau_horaire_1_minute_affichage),
    .Minute_10_affichage(Fuseau_horaire_1_minute_10_affichage),
    .Heure_affichage(Fuseau_horaire_1_heure_affichage),
    .Heure_10_affichage(Fuseau_horaire_1_heure_10_affichage));
endmodule

module Debouncer (
  input  Button,
  output Debounced_button
);

  wire clock_1_out, d_ff_1_q, d_ff_2_q, d_ff_3_q;

  Clock #(.highDuration(640), .lowDuration(640)) clock_1 (.out(clock_1_out));
  D_Flip_Flop d_ff_1 (.D(Button), .clk(clock_1_out), .Q(d_ff_1_q));  // open: Qn, preset, reset
  D_Flip_Flop d_ff_2 (.D(d_ff_1_q), .clk(clock_1_out), .Q(d_ff_2_q));  // open: Qn, preset, reset
  D_Flip_Flop d_ff_3 (.D(d_ff_2_q), .clk(clock_1_out), .Q(d_ff_3_q));  // open: Qn, preset, reset
  and and_1 (Debounced_button, d_ff_1_q, d_ff_2_q, d_ff_3_q);
endmodule

module Segment_A (
  input  W,
  input  X,
  input  Y,
  input  Z,
  output A
);

  wire and_1_out, and_2_out, and_3_out, and_4_out, not_1_out, not_2_out, not_3_out, not_4_out, or_1_out,
       or_2_out, xor_1_out;

  and and_1 (and_1_out, or_1_out, Y);
  or or_1 (or_1_out, not_1_out, X);
  not not_1 (not_1_out, W);
  and and_2 (and_2_out, not_2_out, or_2_out);
  not not_2 (not_2_out, X);
  or or_2 (or_2_out, and_3_out, not_3_out);
  not not_3 (not_3_out, Z);
  and and_3 (and_3_out, W, not_4_out);
  not not_4 (not_4_out, Y);
  and and_4 (and_4_out, X, xor_1_out);
  xor xor_1 (xor_1_out, Z, W);
  or or_3 (A, and_1_out, and_2_out, and_4_out);
endmodule

module Segment_B (
  input  W,
  input  X,
  input  Y,
  input  Z,
  output B
);

  wire and_1_out, and_2_out, and_3_out, not_1_out, not_2_out, not_3_out, not_4_out, xor_1_out, xor_2_out;

  not not_1 (not_1_out, W);
  and and_1 (and_1_out, xor_1_out, Z);
  xor xor_1 (xor_1_out, W, Y);
  and and_2 (and_2_out, not_1_out, not_2_out, xor_2_out);
  not not_2 (not_2_out, Y);
  xor xor_2 (xor_2_out, X, Z);
  and and_3 (and_3_out, not_3_out, not_4_out);
  not not_3 (not_3_out, X);
  not not_4 (not_4_out, Z);
  or or_1 (B, and_1_out, and_2_out, and_3_out);
endmodule

module Segment_C (
  input  W,
  input  X,
  input  Y,
  input  Z,
  output C
);

  wire and_1_out, and_2_out, not_1_out, not_2_out, not_3_out, not_4_out, not_5_out, or_1_out, or_2_out,
       xor_1_out;

  xor xor_1 (xor_1_out, W, X);
  not not_1 (not_1_out, X);
  and and_1 (and_1_out, or_1_out, Z);
  or or_1 (or_1_out, not_1_out, not_2_out);
  not not_2 (not_2_out, W);
  not not_3 (not_3_out, Y);
  and and_2 (and_2_out, not_3_out, or_2_out);
  or or_2 (or_2_out, not_5_out, not_4_out, Z);
  not not_4 (not_4_out, X);
  not not_5 (not_5_out, W);
  or or_3 (C, xor_1_out, and_1_out, and_2_out);
endmodule

module Segment_D (
  input  W,
  input  X,
  input  Y,
  input  Z,
  output D
);

  wire and_1_out, and_2_out, and_3_out, and_4_out, and_5_out, not_1_out, not_2_out, not_3_out, not_4_out,
       not_5_out, or_1_out, xor_1_out;

  and and_1 (and_1_out, W, not_1_out);
  not not_1 (not_1_out, Y);
  and and_2 (and_2_out, xor_1_out, Y);
  xor xor_1 (xor_1_out, X, Z);
  not not_2 (not_2_out, Y);
  and and_3 (and_3_out, not_3_out, or_1_out);
  not not_3 (not_3_out, W);
  or or_1 (or_1_out, and_5_out, and_4_out);
  and and_4 (and_4_out, not_4_out, not_5_out);
  and and_5 (and_5_out, not_2_out, X, Z);
  not not_4 (not_4_out, X);
  not not_5 (not_5_out, Z);
  or or_2 (D, and_1_out, and_2_out, and_3_out);
endmodule

module Segment_E (
  input  W,
  input  X,
  input  Y,
  input  Z,
  output E
);

  wire and_1_out, and_2_out, and_3_out, and_4_out, not_1_out, not_2_out, not_3_out, not_4_out, or_1_out;

  and and_1 (and_1_out, W, not_1_out, X);
  not not_1 (not_1_out, Y);
  and and_2 (and_2_out, or_1_out, Y);
  or or_1 (or_1_out, W, and_3_out);
  and and_3 (and_3_out, not_2_out, X, not_4_out);
  not not_2 (not_2_out, W);
  and and_4 (and_4_out, not_3_out, not_4_out);
  not not_3 (not_3_out, X);
  not not_4 (not_4_out, Z);
  or or_2 (E, and_1_out, and_2_out, and_4_out);
endmodule

module Segment_F (
  input  W,
  input  X,
  input  Y,
  input  Z,
  output F
);

  wire and_1_out, and_2_out, and_3_out, and_4_out, not_1_out, not_2_out, not_3_out, not_4_out, or_1_out,
       or_2_out;

  and and_1 (and_1_out, or_1_out, not_3_out);
  or or_1 (or_1_out, and_2_out, not_4_out);
  and and_2 (and_2_out, not_1_out, X);
  not not_1 (not_1_out, W);
  and and_3 (and_3_out, W, or_2_out);
  or or_2 (or_2_out, not_2_out, Y);
  not not_2 (not_2_out, X);
  not not_3 (not_3_out, Y);
  and and_4 (and_4_out, X, not_4_out);
  not not_4 (not_4_out, Z);
  or or_3 (F, and_1_out, and_3_out, and_4_out);
endmodule

module Segment_G (
  input  W,
  input  X,
  input  Y,
  input  Z,
  output G
);

  wire and_1_out, and_2_out, and_3_out, and_4_out, not_1_out, not_2_out, not_3_out, or_1_out, or_2_out,
       xor_1_out;

  or or_1 (or_1_out, xor_1_out, and_2_out);
  xor xor_1 (xor_1_out, W, X);
  and and_1 (and_1_out, or_1_out, not_1_out);
  and and_2 (and_2_out, W, Z);
  not not_1 (not_1_out, Y);
  and and_3 (and_3_out, Y, or_2_out);
  or or_2 (or_2_out, W, not_2_out, and_4_out);
  not not_2 (not_2_out, X);
  and and_4 (and_4_out, X, not_3_out);
  not not_3 (not_3_out, Z);
  or or_3 (G, and_1_out, and_3_out);
endmodule

module Convertisseur (
  input  [4:0] Input_bus_1,
  output a,
  output b,
  output c,
  output d,
  output e,
  output f,
  output g,
  output dot
);

  Segment_A Segment_A_1 (.W(Input_bus_1[1]), .X(Input_bus_1[2]), .Y(Input_bus_1[3]), .Z(Input_bus_1[4]), .A(a));
  Segment_B Segment_B_1 (.W(Input_bus_1[1]), .X(Input_bus_1[2]), .Y(Input_bus_1[3]), .Z(Input_bus_1[4]), .B(b));
  Segment_C Segment_C_1 (.W(Input_bus_1[1]), .X(Input_bus_1[2]), .Y(Input_bus_1[3]), .Z(Input_bus_1[4]), .C(c));
  Segment_D Segment_D_1 (.W(Input_bus_1[1]), .X(Input_bus_1[2]), .Y(Input_bus_1[3]), .Z(Input_bus_1[4]), .D(d));
  Segment_E Segment_E_1 (.W(Input_bus_1[1]), .X(Input_bus_1[2]), .Y(Input_bus_1[3]), .Z(Input_bus_1[4]), .E(e));
  Segment_F Segment_F_1 (.W(Input_bus_1[1]), .X(Input_bus_1[2]), .Y(Input_bus_1[3]), .Z(Input_bus_1[4]), .F(f));
  Segment_G Segment_G_1 (.W(Input_bus_1[1]), .X(Input_bus_1[2]), .Y(Input_bus_1[3]), .Z(Input_bus_1[4]), .G(g));

  assign dot = Input_bus_1[0];
endmodule

module Affichage_ville_1 (
  input  [1:0] choix_ville,
  input  Activation,
  input  HorlogeA,
  input  HorlogeB,
  input  HorlogeC,
  input  HorlogeD,
  input  HorlogeE,
  input  HorlogeF,
  input  HorlogeG,
  output Aout,
  output Bout,
  output Cout,
  output Dout,
  output Eout,
  output Fout,
  output Gout
);

  wire multiplexer_1_out, multiplexer_2_out, multiplexer_3_out, multiplexer_4_out, multiplexer_5_out,
       multiplexer_6_out, multiplexer_7_out;

  Multiplexer #(.select(2), .enable("false")) multiplexer_1 (
    .in0(1'b0), .in1(1'b1), .in2(1'b0), .in3(1'b0), .out(multiplexer_1_out), .sel(choix_ville));
  Multiplexer #(.select(2), .enable("false")) multiplexer_2 (
    .in0(1'b0), .in1(1'b0), .in2(1'b0), .in3(1'b0), .out(multiplexer_2_out), .sel(choix_ville));
  Multiplexer #(.select(2), .enable("false")) multiplexer_3 (
    .in0(1'b0), .in1(1'b0), .in2(1'b0), .in3(1'b0), .out(multiplexer_3_out), .sel(choix_ville));
  Multiplexer #(.select(2), .enable("false")) multiplexer_4 (
    .in0(1'b0), .in1(1'b0), .in2(1'b0), .in3(1'b0), .out(multiplexer_4_out), .sel(choix_ville));
  Multiplexer #(.select(2), .enable("false")) multiplexer_5 (
    .in0(1'b0), .in1(1'b1), .in2(1'b0), .in3(1'b0), .out(multiplexer_5_out), .sel(choix_ville));
  Multiplexer #(.select(2), .enable("false")) multiplexer_6 (
    .in0(1'b0), .in1(1'b1), .in2(1'b0), .in3(1'b0), .out(multiplexer_6_out), .sel(choix_ville));
  Multiplexer #(.select(2), .enable("false")) multiplexer_7 (
    .in0(1'b0), .in1(1'b0), .in2(1'b0), .in3(1'b0), .out(multiplexer_7_out), .sel(choix_ville));
  Multiplexer #(.enable("false")) multiplexer_8 (.in0(HorlogeA), .in1(multiplexer_1_out), .out(Aout), .sel(Activation));
  Multiplexer #(.enable("false")) multiplexer_9 (.in0(HorlogeB), .in1(multiplexer_2_out), .out(Bout), .sel(Activation));
  Multiplexer #(.enable("false")) multiplexer_10 (
    .in0(HorlogeC), .in1(multiplexer_3_out), .out(Cout), .sel(Activation));
  Multiplexer #(.enable("false")) multiplexer_11 (
    .in0(HorlogeD), .in1(multiplexer_4_out), .out(Dout), .sel(Activation));
  Multiplexer #(.enable("false")) multiplexer_12 (
    .in0(HorlogeE), .in1(multiplexer_5_out), .out(Eout), .sel(Activation));
  Multiplexer #(.enable("false")) multiplexer_13 (
    .in0(HorlogeF), .in1(multiplexer_6_out), .out(Fout), .sel(Activation));
  Multiplexer #(.enable("false")) multiplexer_14 (
    .in0(HorlogeG), .in1(multiplexer_7_out), .out(Gout), .sel(Activation));

  // Notes on the sheet:
  //   Los Angeles 1 A
  //   Los Angeles 1 B
  //   Los Angeles 1 C
  //   Los Angeles 1 D
  //   Los Angeles 1 E
  //   Los Angeles 1 F
  //   Moscou 1 A
  //   Séoul 1 A
  //   Helsinki 1 A
  //   Moscou 1 B
  //   Séoul 1 B
  //   Helsinki 1 B
  //   Moscou 1 C
  //   Séoul 1 C
  //   Helsinki 1 C
  //   Moscou 1 D
  //   Séoul 1 D
  //   Helsinki 1 D
  //   Moscou 1 E
  //   Séoul 1 E
  //   Helsinki 1 E
  //   Moscou 1 F
  //   Séoul 1 F
  //   Helsinki 1 F
  //   Los Angeles 1 G
  //   Moscou 1 G
  //   Séoul 1 G
  //   Helsinki 1 G
endmodule

module Affichage_ville_2 (
  input  [1:0] Choix_ville,
  input  Activation,
  input  HorlogeA,
  input  HorlogeB,
  input  HorlogeC,
  input  HorlogeD,
  input  HorlogeE,
  input  HorlogeF,
  input  HorlogeG,
  output Aout,
  output Bout,
  output Cout,
  output Dout,
  output Eout,
  output Fout,
  output Gout
);

  wire multiplexer_1_out, multiplexer_2_out, multiplexer_3_out, multiplexer_4_out, multiplexer_5_out,
       multiplexer_6_out, multiplexer_7_out;

  Multiplexer #(.select(2), .enable("false")) multiplexer_1 (
    .in0(1'b0), .in1(1'b1), .in2(1'b1), .in3(1'b0), .out(multiplexer_1_out), .sel(Choix_ville));
  Multiplexer #(.select(2), .enable("false")) multiplexer_2 (
    .in0(1'b0), .in1(1'b1), .in2(1'b0), .in3(1'b1), .out(multiplexer_2_out), .sel(Choix_ville));
  Multiplexer #(.select(2), .enable("false")) multiplexer_3 (
    .in0(1'b0), .in1(1'b1), .in2(1'b1), .in3(1'b1), .out(multiplexer_3_out), .sel(Choix_ville));
  Multiplexer #(.select(2), .enable("false")) multiplexer_4 (
    .in0(1'b1), .in1(1'b0), .in2(1'b1), .in3(1'b0), .out(multiplexer_4_out), .sel(Choix_ville));
  Multiplexer #(.select(2), .enable("false")) multiplexer_5 (
    .in0(1'b1), .in1(1'b0), .in2(1'b0), .in3(1'b1), .out(multiplexer_5_out), .sel(Choix_ville));
  Multiplexer #(.select(2), .enable("false")) multiplexer_6 (
    .in0(1'b1), .in1(1'b0), .in2(1'b1), .in3(1'b1), .out(multiplexer_6_out), .sel(Choix_ville));
  Multiplexer #(.select(2), .enable("false")) multiplexer_7 (
    .in0(1'b0), .in1(1'b0), .in2(1'b1), .in3(1'b1), .out(multiplexer_7_out), .sel(Choix_ville));
  Multiplexer #(.enable("false")) multiplexer_8 (.in0(HorlogeA), .in1(multiplexer_1_out), .out(Aout), .sel(Activation));
  Multiplexer #(.enable("false")) multiplexer_9 (.in0(HorlogeB), .in1(multiplexer_2_out), .out(Bout), .sel(Activation));
  Multiplexer #(.enable("false")) multiplexer_10 (
    .in0(HorlogeC), .in1(multiplexer_3_out), .out(Cout), .sel(Activation));
  Multiplexer #(.enable("false")) multiplexer_11 (
    .in0(HorlogeD), .in1(multiplexer_4_out), .out(Dout), .sel(Activation));
  Multiplexer #(.enable("false")) multiplexer_12 (
    .in0(HorlogeE), .in1(multiplexer_5_out), .out(Eout), .sel(Activation));
  Multiplexer #(.enable("false")) multiplexer_13 (
    .in0(HorlogeF), .in1(multiplexer_6_out), .out(Fout), .sel(Activation));
  Multiplexer #(.enable("false")) multiplexer_14 (
    .in0(HorlogeG), .in1(multiplexer_7_out), .out(Gout), .sel(Activation));

  // Notes on the sheet:
  //   Los Angeles 2 A
  //   Los Angeles 2 B
  //   Los Angeles 2 C
  //   Los Angeles 2 D
  //   Los Angeles 2 E
  //   Los Angeles 2 F
  //   Moscou 2 A
  //   Séoul 2 A
  //   Helsinki 2 A
  //   Moscou 2 B
  //   Séoul 2 B
  //   Helsinki 2 B
  //   Moscou 2 C
  //   Séoul 2 C
  //   Helsinki 2 C
  //   Moscou 2 D
  //   Séoul 2 D
  //   Helsinki 2 D
  //   Moscou 2 E
  //   Séoul 2 E
  //   Helsinki 2 E
  //   Moscou 2 F
  //   Séoul 2 F
  //   Helsinki 2 F
  //   Los Angeles 2 G
  //   Moscou 2 G
  //   Séoul 2 G
  //   Helsinki 2 G
endmodule

module Affichage_ville_3 (
  input  [1:0] Choix_ville,
  input  Activation,
  input  HorlogeA,
  input  HorlogeB,
  input  HorlogeC,
  input  HorlogeD,
  input  HorlogeE,
  input  HorlogeF,
  input  HorlogeG,
  output Aout,
  output Bout,
  output Cout,
  output Dout,
  output Eout,
  output Fout,
  output Gout
);

  wire multiplexer_1_out, multiplexer_2_out, multiplexer_3_out, multiplexer_4_out, multiplexer_5_out,
       multiplexer_6_out, multiplexer_7_out;

  Multiplexer #(.select(2), .enable("false")) multiplexer_1 (
    .in0(1'b1), .in1(1'b1), .in2(1'b1), .in3(1'b1), .out(multiplexer_1_out), .sel(Choix_ville));
  Multiplexer #(.select(2), .enable("false")) multiplexer_2 (
    .in0(1'b1), .in1(1'b1), .in2(1'b0), .in3(1'b0), .out(multiplexer_2_out), .sel(Choix_ville));
  Multiplexer #(.select(2), .enable("false")) multiplexer_3 (
    .in0(1'b1), .in1(1'b1), .in2(1'b0), .in3(1'b0), .out(multiplexer_3_out), .sel(Choix_ville));
  Multiplexer #(.select(2), .enable("false")) multiplexer_4 (
    .in0(1'b1), .in1(1'b1), .in2(1'b1), .in3(1'b1), .out(multiplexer_4_out), .sel(Choix_ville));
  Multiplexer #(.select(2), .enable("false")) multiplexer_5 (
    .in0(1'b1), .in1(1'b1), .in2(1'b1), .in3(1'b1), .out(multiplexer_5_out), .sel(Choix_ville));
  Multiplexer #(.select(2), .enable("false")) multiplexer_6 (
    .in0(1'b1), .in1(1'b1), .in2(1'b1), .in3(1'b1), .out(multiplexer_6_out), .sel(Choix_ville));
  Multiplexer #(.select(2), .enable("false")) multiplexer_7 (
    .in0(1'b0), .in1(1'b0), .in2(1'b1), .in3(1'b1), .out(multiplexer_7_out), .sel(Choix_ville));
  Multiplexer #(.enable("false")) multiplexer_8 (.in0(HorlogeA), .in1(multiplexer_1_out), .out(Aout), .sel(Activation));
  Multiplexer #(.enable("false")) multiplexer_9 (.in0(HorlogeB), .in1(multiplexer_2_out), .out(Bout), .sel(Activation));
  Multiplexer #(.enable("false")) multiplexer_10 (
    .in0(HorlogeC), .in1(multiplexer_3_out), .out(Cout), .sel(Activation));
  Multiplexer #(.enable("false")) multiplexer_11 (
    .in0(HorlogeD), .in1(multiplexer_4_out), .out(Dout), .sel(Activation));
  Multiplexer #(.enable("false")) multiplexer_12 (
    .in0(HorlogeE), .in1(multiplexer_5_out), .out(Eout), .sel(Activation));
  Multiplexer #(.enable("false")) multiplexer_13 (
    .in0(HorlogeF), .in1(multiplexer_6_out), .out(Fout), .sel(Activation));
  Multiplexer #(.enable("false")) multiplexer_14 (
    .in0(HorlogeG), .in1(multiplexer_7_out), .out(Gout), .sel(Activation));

  // Notes on the sheet:
  //   Los Angeles 3 A
  //   Los Angeles 3 B
  //   Los Angeles 3 C
  //   Los Angeles 3 D
  //   Los Angeles 3 E
  //   Moscou 3 E
  //   Los Angeles 3 F
  //   Moscou 3 A
  //   Séoul 3 A
  //   Helsinki 3 A
  //   Moscou 3 B
  //   Séoul 3 B
  //   Helsinki 3 B
  //   Moscou 3 C
  //   Séoul 3 C
  //   Helsinki 3 C
  //   Moscou 3 D
  //   Séoul 3 D
  //   Helsinki 3 D
  //   Séoul 3 E
  //   Helsinki 3 E
  //   Moscou 3 F
  //   Séoul 3 F
  //   Helsinki 3 F
  //   Los Angeles 3 G
  //   Moscou 3 G
  //   Séoul 3 G
  //   Helsinki 3 G
endmodule

module Affichage_ville_4 (
  input  [1:0] Choix_ville,
  input  Activation,
  input  HorlogeA,
  input  HorlogeB,
  input  HorlogeC,
  input  HorlogeD,
  input  HorlogeE,
  input  HorlogeF,
  input  HorlogeG,
  output Aout,
  output Bout,
  output Cout,
  output Dout,
  output Eout,
  output Fout,
  output Gout
);

  wire multiplexer_1_out, multiplexer_2_out, multiplexer_3_out, multiplexer_4_out, multiplexer_5_out,
       multiplexer_6_out, multiplexer_7_out;

  Multiplexer #(.select(2), .enable("false")) multiplexer_1 (
    .in0(1'b1), .in1(1'b1), .in2(1'b1), .in3(1'b0), .out(multiplexer_1_out), .sel(Choix_ville));
  Multiplexer #(.select(2), .enable("false")) multiplexer_2 (
    .in0(1'b0), .in1(1'b0), .in2(1'b1), .in3(1'b0), .out(multiplexer_2_out), .sel(Choix_ville));
  Multiplexer #(.select(2), .enable("false")) multiplexer_3 (
    .in0(1'b1), .in1(1'b1), .in2(1'b1), .in3(1'b0), .out(multiplexer_3_out), .sel(Choix_ville));
  Multiplexer #(.select(2), .enable("false")) multiplexer_4 (
    .in0(1'b1), .in1(1'b1), .in2(1'b1), .in3(1'b1), .out(multiplexer_4_out), .sel(Choix_ville));
  Multiplexer #(.select(2), .enable("false")) multiplexer_5 (
    .in0(1'b0), .in1(1'b0), .in2(1'b1), .in3(1'b1), .out(multiplexer_5_out), .sel(Choix_ville));
  Multiplexer #(.select(2), .enable("false")) multiplexer_6 (
    .in0(1'b1), .in1(1'b1), .in2(1'b1), .in3(1'b1), .out(multiplexer_6_out), .sel(Choix_ville));
  Multiplexer #(.select(2), .enable("false")) multiplexer_7 (
    .in0(1'b1), .in1(1'b1), .in2(1'b0), .in3(1'b0), .out(multiplexer_7_out), .sel(Choix_ville));
  Multiplexer #(.enable("false")) multiplexer_8 (.in0(HorlogeA), .in1(multiplexer_1_out), .out(Aout), .sel(Activation));
  Multiplexer #(.enable("false")) multiplexer_9 (.in0(HorlogeB), .in1(multiplexer_2_out), .out(Bout), .sel(Activation));
  Multiplexer #(.enable("false")) multiplexer_10 (
    .in0(HorlogeC), .in1(multiplexer_3_out), .out(Cout), .sel(Activation));
  Multiplexer #(.enable("false")) multiplexer_11 (
    .in0(HorlogeD), .in1(multiplexer_4_out), .out(Dout), .sel(Activation));
  Multiplexer #(.enable("false")) multiplexer_12 (
    .in0(HorlogeE), .in1(multiplexer_5_out), .out(Eout), .sel(Activation));
  Multiplexer #(.enable("false")) multiplexer_13 (
    .in0(HorlogeF), .in1(multiplexer_6_out), .out(Fout), .sel(Activation));
  Multiplexer #(.enable("false")) multiplexer_14 (
    .in0(HorlogeG), .in1(multiplexer_7_out), .out(Gout), .sel(Activation));

  // Notes on the sheet:
  //   Los Angeles 4 A
  //   Los Angeles 4 B
  //   Los Angeles 4 C
  //   Los Angeles 4 D
  //   Los Angeles 4 E
  //   Moscou 4 E
  //   Los Angeles 4 F
  //   Moscou 4 A
  //   Séoul 4 A
  //   Helsinki 4 A
  //   Moscou 4 B
  //   Séoul 4 B
  //   Helsinki 4 B
  //   Moscou 4 C
  //   Séoul 4 C
  //   Helsinki 4 C
  //   Moscou 4 D
  //   Séoul 4 D
  //   Helsinki 4 D
  //   Séoul 4 E
  //   Helsinki 4 E
  //   Moscou 4 F
  //   Séoul 4 F
  //   Helsinki 4 F
  //   Los Angeles 4 G
  //   Moscou 4 G
  //   Séoul 4 G
  //   Helsinki 4 G
endmodule

module Encodeur_LA (
  input  C11,
  input  C01,
  input  C30,
  input  C20,
  input  C10,
  input  C00,
  output D11,
  output D01,
  output D30,
  output D20,
  output D10,
  output D00
);

  wire nand_1_out, nand_2_out, nand_3_out, nand_4_out, nand_5_out, nand_6_out, nand_7_out, nand_8_out,
       nand_9_out, nand_10_out, nand_11_out, nand_12_out, nand_13_out, nand_14_out, nand_15_out, nand_16_out,
       nand_17_out, nand_18_out, nand_19_out, nand_20_out, nand_21_out, nand_22_out, nand_23_out,
       nand_24_out, nand_25_out, nand_26_out, nand_27_out, nand_28_out, nand_29_out, nand_30_out,
       nand_31_out, nand_32_out, nand_33_out, nand_34_out, nand_35_out, nand_36_out, nand_37_out,
       nand_38_out, nand_39_out, nand_40_out, nand_41_out, nand_42_out, nand_43_out, nand_44_out,
       nand_45_out, nand_46_out, nand_47_out, nand_48_out, nand_49_out, nand_50_out, nand_51_out,
       nand_52_out, nand_53_out, nand_54_out, nand_55_out, nand_56_out, nand_57_out, nand_58_out,
       nand_59_out, nand_60_out, nand_61_out, nand_62_out, nand_63_out, nand_64_out, nand_65_out,
       nand_66_out, nand_67_out, nand_68_out, nand_69_out, nand_70_out, nand_71_out, nand_72_out,
       nand_73_out, nand_74_out, nand_75_out, nand_76_out, nand_77_out, nand_78_out, nand_79_out,
       nand_80_out, nand_81_out, nand_82_out, nand_83_out, nand_84_out, nand_85_out, nand_86_out,
       nand_87_out, nand_88_out, nand_89_out, nand_90_out, nand_91_out, nand_92_out, nand_93_out,
       nand_94_out, nand_95_out, nand_96_out, nand_97_out, nand_98_out, nand_99_out, nand_100_out,
       nand_101_out, nand_102_out, nand_103_out, nand_104_out, nand_105_out, nand_106_out, nand_107_out,
       nand_108_out, nand_109_out, nand_110_out, nand_111_out, nand_112_out, nand_113_out;

  nand nand_1 (nand_1_out, C11, C11);
  nand nand_2 (nand_2_out, C01, C01);
  nand nand_3 (nand_3_out, C30, C30);
  nand nand_4 (nand_4_out, C11, C11);
  nand nand_5 (nand_5_out, C01, C01);
  nand nand_6 (nand_6_out, C30, C30);
  nand nand_7 (nand_7_out, C11, C11);
  nand nand_8 (nand_8_out, C01, C01);
  nand nand_9 (nand_9_out, C20, C20);
  nand nand_10 (nand_10_out, C10, C10);
  nand nand_11 (nand_11_out, C00, C00);
  nand nand_12 (nand_12_out, C01, C01);
  nand nand_13 (nand_13_out, C30, C30);
  nand nand_14 (nand_14_out, C20, C20);
  nand nand_15 (nand_15_out, C01, C01);
  nand nand_16 (nand_16_out, C30, C30);
  nand nand_17 (nand_17_out, C10, C10);
  nand nand_18 (nand_18_out, C00, C00);
  nand nand_19 (nand_19_out, C11, C11);
  nand nand_20 (nand_20_out, C01, C01);
  nand nand_21 (nand_21_out, C30, C30);
  nand nand_22 (nand_22_out, C20, C20);
  nand nand_23 (nand_23_out, C11, C11);
  nand nand_24 (nand_24_out, C01, C01);
  nand nand_25 (nand_25_out, C30, C30);
  nand nand_26 (nand_26_out, C10, C10);
  nand nand_27 (nand_27_out, C00, C00);
  nand nand_28 (nand_28_out, C11, C11);
  nand nand_29 (nand_29_out, C30, C30);
  nand nand_30 (nand_30_out, C11, C11);
  nand nand_31 (nand_31_out, C20, C20);
  nand nand_32 (nand_32_out, C10, C10);
  nand nand_33 (nand_33_out, C00, C00);
  nand nand_34 (nand_34_out, C11, C11);
  nand nand_35 (nand_35_out, C01, C01);
  nand nand_36 (nand_36_out, C30, C30);
  nand nand_37 (nand_37_out, C20, C20);
  nand nand_38 (nand_38_out, C10, C10);
  nand nand_39 (nand_39_out, C11, C11);
  nand nand_40 (nand_40_out, C01, C01);
  nand nand_41 (nand_41_out, C30, C30);
  nand nand_42 (nand_42_out, C20, C20);
  nand nand_43 (nand_43_out, C00, C00);
  nand nand_44 (nand_44_out, C30, C30);
  nand nand_45 (nand_45_out, C20, C20);
  nand nand_46 (nand_46_out, C30, C30);
  nand nand_47 (nand_47_out, C10, C10);
  nand nand_48 (nand_48_out, C30, C30);
  nand nand_49 (nand_49_out, C00, C00);
  nand nand_50 (nand_50_out, C01, C01);
  nand nand_51 (nand_51_out, C30, C30);
  nand nand_52 (nand_52_out, C20, C20);
  nand nand_53 (nand_53_out, C10, C10);
  nand nand_54 (nand_54_out, C01, C01);
  nand nand_55 (nand_55_out, C30, C30);
  nand nand_56 (nand_56_out, C20, C20);
  nand nand_57 (nand_57_out, C00, C00);
  nand nand_58 (nand_58_out, C11, C11);
  nand nand_59 (nand_59_out, C01, C01);
  nand nand_60 (nand_60_out, C30, C30);
  nand nand_61 (nand_61_out, C11, C11);
  nand nand_62 (nand_62_out, C01, C01);
  nand nand_63 (nand_63_out, C20, C20);
  nand nand_64 (nand_64_out, C10, C10);
  nand nand_65 (nand_65_out, C00, C00);
  nand nand_66 (nand_66_out, C11, C11);
  nand nand_67 (nand_67_out, C30, C30);
  nand nand_68 (nand_68_out, C10, C10);
  nand nand_69 (nand_69_out, C11, C11);
  nand nand_70 (nand_70_out, C30, C30);
  nand nand_71 (nand_71_out, C00, C00);
  nand nand_72 (nand_72_out, C11, C11);
  nand nand_73 (nand_73_out, C30, C30);
  nand nand_74 (nand_74_out, C00, C00);
  nand nand_75 (nand_75_out, C11, C11);
  nand nand_76 (nand_76_out, C20, C20);
  nand nand_77 (nand_77_out, C10, C10);
  nand nand_78 (nand_78_out, C00, C00);
  nand nand_79 (nand_79_out, C01, C01);
  nand nand_80 (nand_80_out, C30, C30);
  nand nand_81 (nand_81_out, C20, C20);
  nand nand_82 (nand_82_out, C00, C00);
  nand nand_83 (nand_83_out, nand_1_out, nand_2_out, nand_3_out, C20, C00);
  nand nand_84 (nand_84_out, nand_4_out, nand_5_out, nand_6_out, C20, C10);
  nand nand_85 (nand_85_out, nand_7_out, nand_8_out, C30, nand_9_out, nand_10_out, nand_11_out);
  nand nand_86 (nand_86_out, nand_12_out, nand_13_out, nand_14_out);
  nand nand_87 (nand_87_out, nand_15_out, nand_16_out, nand_17_out, nand_18_out);
  nand nand_88 (nand_88_out, C01, C30, C00);
  nand nand_89 (nand_89_out, C01, C30, C10);
  nand nand_90 (nand_90_out, C01, C30, C20);
  nand nand_91 (nand_91_out, C11, C11);
  nand nand_92 (nand_92_out, nand_19_out, nand_20_out, nand_21_out, nand_22_out, C10, C00);
  nand nand_93 (nand_93_out, nand_23_out, nand_24_out, nand_25_out, C20, nand_26_out, nand_27_out);
  nand nand_94 (nand_94_out, nand_28_out, C01, nand_29_out, C20, C10, C00);
  nand nand_95 (nand_95_out, nand_30_out, C01, C30, nand_31_out, nand_32_out, nand_33_out);
  nand nand_96 (nand_96_out, nand_34_out, nand_35_out, nand_36_out, nand_37_out, nand_38_out);
  nand nand_97 (nand_97_out, nand_39_out, nand_40_out, nand_41_out, nand_42_out, nand_43_out);
  nand nand_98 (nand_98_out, C01, nand_44_out, nand_45_out, C10, C00);
  nand nand_99 (nand_99_out, C01, nand_46_out, C20, nand_47_out);
  nand nand_100 (nand_100_out, C01, nand_48_out, C20, nand_49_out);
  nand nand_101 (nand_101_out, C11, C10, C00);
  nand nand_102 (nand_102_out, C11, C20);
  nand nand_103 (nand_103_out, C11, C30);
  nand nand_104 (nand_104_out, C11, C01);
  nand nand_105 (nand_105_out, nand_50_out, nand_51_out, nand_52_out, nand_53_out, C00);
  nand nand_106 (nand_106_out, nand_54_out, nand_55_out, nand_56_out, C10, nand_57_out);
  nand nand_107 (nand_107_out, nand_58_out, nand_59_out, nand_60_out, C20, C10, C00);
  nand nand_108 (nand_108_out, nand_61_out, nand_62_out, C30, nand_63_out, nand_64_out, nand_65_out);
  nand nand_109 (nand_109_out, nand_66_out, C01, nand_67_out, nand_68_out, C00);
  nand nand_110 (nand_110_out, nand_69_out, C01, nand_70_out, C10, nand_71_out);
  nand nand_111 (nand_111_out, nand_72_out, nand_73_out, nand_74_out);
  nand nand_112 (nand_112_out, nand_75_out, nand_76_out, nand_77_out, nand_78_out);
  nand nand_113 (nand_113_out, nand_79_out, nand_80_out, nand_81_out, nand_82_out);
  nand nand_114 (D11, nand_83_out, nand_84_out, nand_85_out);
  nand nand_115 (D01, nand_86_out, nand_87_out, nand_88_out, nand_89_out, nand_90_out, nand_91_out);
  nand nand_116 (D30, nand_92_out, nand_93_out, nand_94_out, nand_95_out);
  nand nand_117 (D20, nand_96_out, nand_97_out, nand_98_out, nand_99_out, nand_100_out, nand_101_out, nand_102_out, nand_103_out, nand_104_out);
  nand nand_118 (D10, nand_105_out, nand_106_out, nand_107_out, nand_108_out, nand_109_out, nand_110_out);
  nand nand_119 (D00, nand_111_out, nand_112_out, nand_113_out);
endmodule

module Encodeur_Moscow (
  input  C11,
  input  C01,
  input  C30,
  input  C20,
  input  C10,
  input  C00,
  output D11,
  output D01,
  output D30,
  output D20,
  output D10,
  output D00
);

  wire nand_1_out, nand_2_out, nand_3_out, nand_4_out, nand_5_out, nand_6_out, nand_7_out, nand_8_out,
       nand_9_out, nand_10_out, nand_11_out, nand_12_out, nand_13_out, nand_14_out, nand_15_out, nand_16_out,
       nand_17_out, nand_18_out, nand_19_out, nand_20_out, nand_21_out, nand_22_out, nand_23_out,
       nand_24_out, nand_25_out, nand_26_out, nand_27_out, nand_28_out, nand_29_out, nand_30_out,
       nand_31_out, nand_32_out, nand_33_out, nand_34_out, nand_35_out, nand_36_out, nand_37_out,
       nand_38_out, nand_39_out;

  nand nand_1 (nand_1_out, C11, C11);
  nand nand_2 (nand_2_out, C01, C01);
  nand nand_3 (nand_3_out, C30, C30);
  nand nand_4 (nand_4_out, C20, C20);
  nand nand_5 (nand_5_out, C10, C10);
  nand nand_6 (nand_6_out, C11, C11);
  nand nand_7 (nand_7_out, C01, C01);
  nand nand_8 (nand_8_out, C11, C11);
  nand nand_9 (nand_9_out, C30, C30);
  nand nand_10 (nand_10_out, C11, C11);
  nand nand_11 (nand_11_out, C30, C30);
  nand nand_12 (nand_12_out, C11, C11);
  nand nand_13 (nand_13_out, C30, C30);
  nand nand_14 (nand_14_out, C20, C20);
  nand nand_15 (nand_15_out, C11, C11);
  nand nand_16 (nand_16_out, C30, C30);
  nand nand_17 (nand_17_out, C10, C10);
  nand nand_18 (nand_18_out, C11, C11);
  nand nand_19 (nand_19_out, C30, C30);
  nand nand_20 (nand_20_out, C10, C10);
  nand nand_21 (nand_21_out, C01, C01);
  nand nand_22 (nand_22_out, C30, C30);
  nand nand_23 (nand_23_out, C20, C20);
  nand nand_24 (nand_24_out, C10, C10);
  nand nand_25 (nand_25_out, C00, C00);
  nand nand_26 (nand_26_out, C30, C10);
  nand nand_27 (nand_27_out, C30, C20);
  nand nand_28 (nand_28_out, C11, C20);
  nand nand_29 (nand_29_out, C11, C30);
  nand nand_30 (nand_30_out, C11, C01);
  nand nand_31 (nand_31_out, nand_1_out, C01, C30);
  nand nand_32 (nand_32_out, C11, nand_2_out, nand_3_out, nand_4_out, nand_5_out);
  nand nand_33 (nand_33_out, nand_6_out, nand_7_out, C30);
  nand nand_34 (nand_34_out, nand_8_out, C01, nand_9_out);
  nand nand_35 (nand_35_out, nand_10_out, nand_11_out, C20, C10);
  nand nand_36 (nand_36_out, nand_12_out, nand_13_out, nand_14_out, C10);
  nand nand_37 (nand_37_out, nand_15_out, nand_16_out, C20, nand_17_out);
  nand nand_38 (nand_38_out, nand_18_out, nand_19_out, nand_20_out);
  nand nand_39 (nand_39_out, nand_21_out, nand_22_out, nand_23_out, nand_24_out);
  nand nand_40 (D00, nand_25_out, nand_26_out, nand_27_out, nand_28_out, nand_29_out, nand_30_out);
  nand nand_41 (D11, nand_31_out, nand_32_out);
  nand nand_42 (D01, nand_33_out, nand_34_out);
  nand nand_43 (D30, nand_35_out, nand_35_out);
  nand nand_44 (D20, nand_36_out, nand_37_out);
  nand nand_45 (D10, nand_38_out, nand_39_out);
endmodule

module Encodeur_Seoul (
  input  C11,
  input  C01,
  input  C30,
  input  C20,
  input  C10,
  input  C00,
  output D11,
  output D01,
  output D30,
  output D20,
  output D10,
  output D00
);

  wire nand_1_out, nand_2_out, nand_3_out, nand_4_out, nand_5_out, nand_6_out, nand_7_out, nand_8_out,
       nand_9_out, nand_10_out, nand_11_out, nand_12_out, nand_13_out, nand_14_out, nand_15_out, nand_16_out,
       nand_17_out, nand_18_out, nand_19_out, nand_20_out, nand_21_out, nand_22_out, nand_23_out,
       nand_24_out, nand_25_out, nand_26_out, nand_27_out, nand_28_out, nand_29_out, nand_30_out,
       nand_31_out, nand_32_out, nand_33_out, nand_34_out, nand_35_out, nand_36_out, nand_37_out,
       nand_38_out, nand_39_out, nand_40_out, nand_41_out, nand_42_out, nand_43_out;

  nand nand_1 (nand_1_out, C11, C11);
  nand nand_2 (nand_2_out, C30, C30);
  nand nand_3 (nand_3_out, C20, C20);
  nand nand_4 (nand_4_out, C11, C11);
  nand nand_5 (nand_5_out, C30, C30);
  nand nand_6 (nand_6_out, C10, C10);
  nand nand_7 (nand_7_out, C11, C11);
  nand nand_8 (nand_8_out, C01, C01);
  nand nand_9 (nand_9_out, C11, C11);
  nand nand_10 (nand_10_out, C01, C01);
  nand nand_11 (nand_11_out, C11, C11);
  nand nand_12 (nand_12_out, C01, C01);
  nand nand_13 (nand_13_out, C11, C11);
  nand nand_14 (nand_14_out, C30, C30);
  nand nand_15 (nand_15_out, C20, C20);
  nand nand_16 (nand_16_out, C10, C10);
  nand nand_17 (nand_17_out, C11, C11);
  nand nand_18 (nand_18_out, C30, C30);
  nand nand_19 (nand_19_out, C20, C20);
  nand nand_20 (nand_20_out, C10, C10);
  nand nand_21 (nand_21_out, C01, C01);
  nand nand_22 (nand_22_out, C01, C01);
  nand nand_23 (nand_23_out, C10, C10);
  nand nand_24 (nand_24_out, C00, C00);
  nand nand_25 (nand_25_out, C30, C10);
  nand nand_26 (nand_26_out, C30, C20);
  nand nand_27 (nand_27_out, C11, C20);
  nand nand_28 (nand_28_out, C11, C30);
  nand nand_29 (nand_29_out, C11, C01);
  nand nand_30 (nand_30_out, nand_1_out, C01, nand_2_out, nand_3_out, C10);
  nand nand_31 (nand_31_out, nand_4_out, C01, nand_5_out, C20, nand_6_out);
  nand nand_32 (nand_32_out, nand_7_out, nand_8_out, C10);
  nand nand_33 (nand_33_out, nand_9_out, nand_10_out, C20);
  nand nand_34 (nand_34_out, nand_11_out, nand_12_out, C30);
  nand nand_35 (nand_35_out, nand_13_out, C01, nand_14_out, nand_15_out, nand_16_out);
  nand nand_36 (nand_36_out, nand_17_out, nand_18_out, nand_19_out, nand_20_out);
  nand nand_37 (nand_37_out, nand_21_out, C20, C10);
  nand nand_38 (nand_38_out, nand_22_out, C30);
  nand nand_39 (nand_39_out, C11, C11);
  nand nand_40 (nand_40_out, C20, nand_23_out);
  nand nand_41 (nand_41_out, C30, C30);
  nand nand_42 (nand_42_out, C11, C10);
  nand nand_43 (nand_43_out, C11, C01);
  nand nand_44 (D00, nand_24_out, nand_25_out, nand_26_out, nand_27_out, nand_28_out, nand_29_out);
  nand nand_45 (D11, nand_30_out, nand_31_out);
  nand nand_46 (D01, nand_32_out, nand_33_out, nand_34_out, nand_35_out);
  nand nand_47 (D30, nand_36_out, nand_36_out);
  nand nand_48 (D20, nand_37_out, nand_38_out, nand_39_out);
  nand nand_49 (D10, nand_40_out, nand_41_out, nand_42_out, nand_43_out);
endmodule

module Encodeur_Helsinki (
  input  C11,
  input  C01,
  input  C30,
  input  C20,
  input  C10,
  input  C00,
  output D11,
  output D01,
  output D30,
  output D20,
  output D10,
  output D00
);

  wire nand_1_out, nand_2_out, nand_3_out, nand_4_out, nand_5_out, nand_6_out, nand_7_out, nand_8_out,
       nand_9_out, nand_10_out, nand_11_out, nand_12_out, nand_13_out, nand_14_out, nand_15_out, nand_16_out,
       nand_17_out, nand_18_out, nand_19_out, nand_20_out, nand_21_out, nand_22_out, nand_23_out,
       nand_24_out, nand_25_out, nand_26_out, nand_27_out, nand_28_out, nand_29_out, nand_30_out,
       nand_31_out, nand_32_out, nand_33_out, nand_34_out, nand_35_out, nand_36_out, nand_37_out,
       nand_38_out, nand_39_out, nand_40_out, nand_41_out, nand_42_out, nand_43_out, nand_44_out,
       nand_45_out, nand_46_out, nand_47_out, nand_48_out, nand_49_out, nand_50_out, nand_51_out,
       nand_52_out, nand_53_out, nand_54_out, nand_55_out, nand_56_out, nand_57_out, nand_58_out,
       nand_59_out, nand_60_out, nand_61_out, nand_62_out, nand_63_out, nand_64_out, nand_65_out,
       nand_66_out, nand_67_out, nand_68_out, nand_69_out, nand_70_out, nand_71_out, nand_72_out,
       nand_73_out, nand_74_out, nand_75_out, nand_76_out, nand_77_out, nand_78_out, nand_79_out,
       nand_80_out, nand_81_out, nand_82_out, nand_83_out, nand_84_out, nand_85_out;

  nand nand_1 (nand_1_out, C11, C11);
  nand nand_2 (nand_2_out, C11, C11);
  nand nand_3 (nand_3_out, C11, C11);
  nand nand_4 (nand_4_out, C01, C01);
  nand nand_5 (nand_5_out, C30, C30);
  nand nand_6 (nand_6_out, C20, C20);
  nand nand_7 (nand_7_out, C10, C10);
  nand nand_8 (nand_8_out, C01, C01);
  nand nand_9 (nand_9_out, C30, C30);
  nand nand_10 (nand_10_out, C20, C20);
  nand nand_11 (nand_11_out, C00, C00);
  nand nand_12 (nand_12_out, C11, C11);
  nand nand_13 (nand_13_out, C01, C01);
  nand nand_14 (nand_14_out, C11, C11);
  nand nand_15 (nand_15_out, C01, C01);
  nand nand_16 (nand_16_out, C11, C11);
  nand nand_17 (nand_17_out, C01, C01);
  nand nand_18 (nand_18_out, C11, C11);
  nand nand_19 (nand_19_out, C30, C30);
  nand nand_20 (nand_20_out, C11, C11);
  nand nand_21 (nand_21_out, C20, C20);
  nand nand_22 (nand_22_out, C10, C10);
  nand nand_23 (nand_23_out, C00, C00);
  nand nand_24 (nand_24_out, C11, C11);
  nand nand_25 (nand_25_out, C30, C30);
  nand nand_26 (nand_26_out, C11, C11);
  nand nand_27 (nand_27_out, C20, C20);
  nand nand_28 (nand_28_out, C10, C10);
  nand nand_29 (nand_29_out, C00, C00);
  nand nand_30 (nand_30_out, C11, C11);
  nand nand_31 (nand_31_out, C30, C30);
  nand nand_32 (nand_32_out, C20, C20);
  nand nand_33 (nand_33_out, C11, C11);
  nand nand_34 (nand_34_out, C30, C30);
  nand nand_35 (nand_35_out, C10, C10);
  nand nand_36 (nand_36_out, C11, C11);
  nand nand_37 (nand_37_out, C30, C30);
  nand nand_38 (nand_38_out, C00, C00);
  nand nand_39 (nand_39_out, C11, C11);
  nand nand_40 (nand_40_out, C30, C30);
  nand nand_41 (nand_41_out, C10, C10);
  nand nand_42 (nand_42_out, C01, C01);
  nand nand_43 (nand_43_out, C30, C30);
  nand nand_44 (nand_44_out, C20, C20);
  nand nand_45 (nand_45_out, C10, C10);
  nand nand_46 (nand_46_out, C11, C11);
  nand nand_47 (nand_47_out, C30, C30);
  nand nand_48 (nand_48_out, C00, C00);
  nand nand_49 (nand_49_out, C01, C01);
  nand nand_50 (nand_50_out, C30, C30);
  nand nand_51 (nand_51_out, C20, C20);
  nand nand_52 (nand_52_out, C00, C00);
  nand nand_53 (nand_53_out, C11, C11);
  nand nand_54 (nand_54_out, C30, C30);
  nand nand_55 (nand_55_out, C00, C00);
  nand nand_56 (nand_56_out, C11, C11);
  nand nand_57 (nand_57_out, C20, C20);
  nand nand_58 (nand_58_out, C10, C10);
  nand nand_59 (nand_59_out, C00, C00);
  nand nand_60 (nand_60_out, C01, C01);
  nand nand_61 (nand_61_out, C30, C30);
  nand nand_62 (nand_62_out, C20, C20);
  nand nand_63 (nand_63_out, C00, C00);
  nand nand_64 (nand_64_out, nand_1_out, C01, C30, C00);
  nand nand_65 (nand_65_out, nand_2_out, C01, C30, C10);
  nand nand_66 (nand_66_out, nand_3_out, C01, C30, C20);
  nand nand_67 (nand_67_out, C11, nand_4_out, nand_5_out, nand_6_out, nand_7_out);
  nand nand_68 (nand_68_out, C11, nand_8_out, nand_9_out, nand_10_out, nand_11_out);
  nand nand_69 (nand_69_out, nand_12_out, nand_13_out, C30, C00);
  nand nand_70 (nand_70_out, nand_14_out, nand_15_out, C30, C10);
  nand nand_71 (nand_71_out, nand_16_out, nand_17_out, C30, C20);
  nand nand_72 (nand_72_out, nand_18_out, C01, nand_19_out);
  nand nand_73 (nand_73_out, nand_20_out, C01, nand_21_out, nand_22_out, nand_23_out);
  nand nand_74 (nand_74_out, nand_24_out, nand_25_out, C20, C10, C00);
  nand nand_75 (nand_75_out, nand_26_out, C30, nand_27_out, nand_28_out, nand_29_out);
  nand nand_76 (nand_76_out, nand_30_out, nand_31_out, nand_32_out, C10, C00);
  nand nand_77 (nand_77_out, nand_33_out, nand_34_out, C20, nand_35_out);
  nand nand_78 (nand_78_out, nand_36_out, nand_37_out, C20, nand_38_out);
  nand nand_79 (nand_79_out, nand_39_out, nand_40_out, nand_41_out, C00);
  nand nand_80 (nand_80_out, nand_42_out, nand_43_out, nand_44_out, nand_45_out, C00);
  nand nand_81 (nand_81_out, nand_46_out, nand_47_out, C10, nand_48_out);
  nand nand_82 (nand_82_out, nand_49_out, nand_50_out, nand_51_out, C10, nand_52_out);
  nand nand_83 (nand_83_out, nand_53_out, nand_54_out, nand_55_out);
  nand nand_84 (nand_84_out, nand_56_out, nand_57_out, nand_58_out, nand_59_out);
  nand nand_85 (nand_85_out, nand_60_out, nand_61_out, nand_62_out, nand_63_out);
  nand nand_86 (D11, nand_64_out, nand_65_out, nand_66_out, nand_67_out, nand_68_out);
  nand nand_87 (D01, nand_69_out, nand_70_out, nand_71_out, nand_72_out, nand_73_out);
  nand nand_88 (D30, nand_74_out, nand_75_out);
  nand nand_89 (D20, nand_76_out, nand_77_out, nand_78_out);
  nand nand_90 (D10, nand_79_out, nand_80_out, nand_81_out, nand_82_out);
  nand nand_91 (D00, nand_83_out, nand_84_out, nand_85_out);
endmodule

module Encodeur_choix_Ville (
  input  Bouton,
  input  Reset,
  output [1:0] Output_bus_1
);

  wire Ajouteur_4554604f_1_carry_out, Ajouteur_4554604f_1_resultat, Ajouteur_4554604f_2_resultat, clock_1_out;

  Clock #(.highDuration(17000), .lowDuration(17000)) clock_1 (.out(clock_1_out));
  Ajouteur_0a5b1135 Ajouteur_4554604f_1 (
    .a(Output_bus_1[0]), .b(Bouton), .carry_in(1'b0), .resultat(Ajouteur_4554604f_1_resultat),
    .carry_out(Ajouteur_4554604f_1_carry_out));
  D_Flip_Flop d_ff_1 (
    .D(Ajouteur_4554604f_1_resultat), .clk(clock_1_out), .Q(Output_bus_1[0]), .reset(Reset));  // open: Qn, preset
  Ajouteur_0a5b1135 Ajouteur_4554604f_2 (
    .a(Output_bus_1[1]), .b(Ajouteur_4554604f_1_carry_out), .carry_in(1'b0),
    .resultat(Ajouteur_4554604f_2_resultat));  // open: carry_out
  D_Flip_Flop d_ff_2 (
    .D(Ajouteur_4554604f_2_resultat), .clk(clock_1_out), .Q(Output_bus_1[1]), .reset(Reset));  // open: Qn, preset
endmodule

module Fuseau_horaire (
  input  [29:0] Heure,
  input  [2:0] Fuseau_horaire_in,
  output [7:0] Seconde_affichage,
  output [7:0] Seconde_10_affichage,
  output [7:0] Minute_affichage,
  output [7:0] Minute_10_affichage,
  output [7:0] Heure_affichage,
  output [7:0] Heure_10_affichage
);

  wire Convertisseur_1_a, Convertisseur_1_b, Convertisseur_1_c, Convertisseur_1_d, Convertisseur_1_e,
       Convertisseur_1_f, Convertisseur_1_g, Convertisseur_2_a, Convertisseur_2_b, Convertisseur_2_c,
       Convertisseur_2_d, Convertisseur_2_e, Convertisseur_2_f, Convertisseur_2_g, Convertisseur_3_a,
       Convertisseur_3_b, Convertisseur_3_c, Convertisseur_3_d, Convertisseur_3_e, Convertisseur_3_f,
       Convertisseur_3_g, Convertisseur_4_a, Convertisseur_4_b, Convertisseur_4_c, Convertisseur_4_d,
       Convertisseur_4_e, Convertisseur_4_f, Convertisseur_4_g;
  wire [1:0] Encodeur_choix_Ville_1_output_bus_1;
  wire [9:0] demultiplexer_1_out0, demultiplexer_1_out1, demultiplexer_2_out0_2, demultiplexer_2_out1_2,
       demultiplexer_2_out2_2, demultiplexer_2_out3_2, multiplexer_1_out, multiplexer_2_out;
  wire [9:1] demultiplexer_2_out0, demultiplexer_2_out1, demultiplexer_2_out2, demultiplexer_2_out3;

  Demultiplexer #(.width(10), .enable("false")) demultiplexer_1 (
    .out0(demultiplexer_1_out0), .out1(demultiplexer_1_out1), .in(Heure[29:20]), .sel(Fuseau_horaire_in[1]));
  Demultiplexer #(.select(2), .width(10), .enable("false")) demultiplexer_2 (
    .out0({demultiplexer_2_out0[9:8], demultiplexer_2_out0_2[7:5], demultiplexer_2_out0[4:1], demultiplexer_2_out0_2[0]}),
    .out1({demultiplexer_2_out1[9:8], demultiplexer_2_out1_2[7:5], demultiplexer_2_out1[4:1], demultiplexer_2_out1_2[0]}),
    .out2({demultiplexer_2_out2[9:8], demultiplexer_2_out2_2[7:5], demultiplexer_2_out2[4:1], demultiplexer_2_out2_2[0]}),
    .out3({demultiplexer_2_out3[9:8], demultiplexer_2_out3_2[7:5], demultiplexer_2_out3[4:1], demultiplexer_2_out3_2[0]}),
    .in(demultiplexer_1_out1), .sel(Encodeur_choix_Ville_1_output_bus_1));
  Encodeur_choix_Ville Encodeur_choix_Ville_1 (
    .Bouton(Fuseau_horaire_in[2]), .Reset(Fuseau_horaire_in[0]),
    .Output_bus_1(Encodeur_choix_Ville_1_output_bus_1));
  Encodeur_LA Encodeur_LA_1 (
    .C11(demultiplexer_2_out0[8]), .C01(demultiplexer_2_out0[9]), .C30(demultiplexer_2_out0[1]),
    .C20(demultiplexer_2_out0[2]), .C10(demultiplexer_2_out0[3]), .C00(demultiplexer_2_out0[4]),
    .D11(demultiplexer_2_out0_2[8]), .D01(demultiplexer_2_out0_2[9]), .D30(demultiplexer_2_out0_2[1]),
    .D20(demultiplexer_2_out0_2[2]), .D10(demultiplexer_2_out0_2[3]), .D00(demultiplexer_2_out0_2[4]));
  Encodeur_Moscow Encodeur_Moscow_1 (
    .C11(demultiplexer_2_out1[8]), .C01(demultiplexer_2_out1[9]), .C30(demultiplexer_2_out1[1]),
    .C20(demultiplexer_2_out1[2]), .C10(demultiplexer_2_out1[3]), .C00(demultiplexer_2_out1[4]),
    .D11(demultiplexer_2_out1_2[8]), .D01(demultiplexer_2_out1_2[9]), .D30(demultiplexer_2_out1_2[1]),
    .D20(demultiplexer_2_out1_2[2]), .D10(demultiplexer_2_out1_2[3]), .D00(demultiplexer_2_out1_2[4]));
  Encodeur_Seoul Encodeur_Seoul_1 (
    .C11(demultiplexer_2_out2[8]), .C01(demultiplexer_2_out2[9]), .C30(demultiplexer_2_out2[1]),
    .C20(demultiplexer_2_out2[2]), .C10(demultiplexer_2_out2[3]), .C00(demultiplexer_2_out2[4]),
    .D11(demultiplexer_2_out2_2[8]), .D01(demultiplexer_2_out2_2[9]), .D30(demultiplexer_2_out2_2[1]),
    .D20(demultiplexer_2_out2_2[2]), .D10(demultiplexer_2_out2_2[3]), .D00(demultiplexer_2_out2_2[4]));
  Encodeur_Helsinki Encodeur_Helsinki_1 (
    .C11(demultiplexer_2_out3[8]), .C01(demultiplexer_2_out3[9]), .C30(demultiplexer_2_out3[1]),
    .C20(demultiplexer_2_out3[2]), .C10(demultiplexer_2_out3[3]), .C00(demultiplexer_2_out3[4]),
    .D11(demultiplexer_2_out3_2[8]), .D01(demultiplexer_2_out3_2[9]), .D30(demultiplexer_2_out3_2[1]),
    .D20(demultiplexer_2_out3_2[2]), .D10(demultiplexer_2_out3_2[3]), .D00(demultiplexer_2_out3_2[4]));
  Multiplexer #(.select(2), .width(10), .enable("false")) multiplexer_1 (
    .in0(demultiplexer_2_out0_2), .in1(demultiplexer_2_out1_2), .in2(demultiplexer_2_out2_2),
    .in3(demultiplexer_2_out3_2), .out(multiplexer_1_out), .sel(Encodeur_choix_Ville_1_output_bus_1));
  Multiplexer #(.width(10), .enable("false")) multiplexer_2 (
    .in0(demultiplexer_1_out0), .in1(multiplexer_1_out), .out(multiplexer_2_out), .sel(Fuseau_horaire_in[1]));
  Convertisseur Convertisseur_1 (
    .Input_bus_1(Heure[4:0]), .a(Convertisseur_1_a), .b(Convertisseur_1_b), .c(Convertisseur_1_c),
    .d(Convertisseur_1_d), .e(Convertisseur_1_e), .f(Convertisseur_1_f), .g(Convertisseur_1_g),
    .dot(Seconde_affichage[7]));
  Convertisseur Convertisseur_2 (
    .Input_bus_1(Heure[9:5]), .a(Convertisseur_2_a), .b(Convertisseur_2_b), .c(Convertisseur_2_c),
    .d(Convertisseur_2_d), .e(Convertisseur_2_e), .f(Convertisseur_2_f), .g(Convertisseur_2_g),
    .dot(Seconde_10_affichage[7]));
  Convertisseur Convertisseur_3 (
    .Input_bus_1(Heure[14:10]), .a(Convertisseur_3_a), .b(Convertisseur_3_b), .c(Convertisseur_3_c),
    .d(Convertisseur_3_d), .e(Convertisseur_3_e), .f(Convertisseur_3_f), .g(Convertisseur_3_g),
    .dot(Minute_affichage[7]));
  Convertisseur Convertisseur_4 (
    .Input_bus_1(Heure[19:15]), .a(Convertisseur_4_a), .b(Convertisseur_4_b), .c(Convertisseur_4_c),
    .d(Convertisseur_4_d), .e(Convertisseur_4_e), .f(Convertisseur_4_f), .g(Convertisseur_4_g),
    .dot(Minute_10_affichage[7]));
  Convertisseur Convertisseur_5 (
    .Input_bus_1(multiplexer_2_out[4:0]), .a(Heure_affichage[0]), .b(Heure_affichage[1]),
    .c(Heure_affichage[2]), .d(Heure_affichage[3]), .e(Heure_affichage[4]), .f(Heure_affichage[5]),
    .g(Heure_affichage[6]), .dot(Heure_affichage[7]));
  Convertisseur Convertisseur_6 (
    .Input_bus_1(multiplexer_2_out[9:5]), .a(Heure_10_affichage[0]), .b(Heure_10_affichage[1]),
    .c(Heure_10_affichage[2]), .d(Heure_10_affichage[3]), .e(Heure_10_affichage[4]),
    .f(Heure_10_affichage[5]), .g(Heure_10_affichage[6]), .dot(Heure_10_affichage[7]));
  Affichage_ville_1 Affichage_ville_1_1 (
    .HorlogeA(Convertisseur_4_a), .HorlogeB(Convertisseur_4_b), .HorlogeG(Convertisseur_4_g),
    .HorlogeD(Convertisseur_4_d), .HorlogeF(Convertisseur_4_f), .HorlogeE(Convertisseur_4_e),
    .Fout(Minute_10_affichage[5]), .Dout(Minute_10_affichage[3]), .Cout(Minute_10_affichage[2]),
    .HorlogeC(Convertisseur_4_c), .Aout(Minute_10_affichage[0]), .Bout(Minute_10_affichage[1]),
    .Eout(Minute_10_affichage[4]), .choix_ville(Encodeur_choix_Ville_1_output_bus_1),
    .Gout(Minute_10_affichage[6]), .Activation(Fuseau_horaire_in[1]));
  Affichage_ville_2 Affichage_ville_2_1 (
    .HorlogeD(Convertisseur_3_d), .HorlogeA(Convertisseur_3_a), .HorlogeG(Convertisseur_3_g),
    .HorlogeE(Convertisseur_3_e), .Bout(Minute_affichage[1]), .HorlogeC(Convertisseur_3_c),
    .Cout(Minute_affichage[2]), .Aout(Minute_affichage[0]), .HorlogeF(Convertisseur_3_f),
    .Choix_ville(Encodeur_choix_Ville_1_output_bus_1), .HorlogeB(Convertisseur_3_b),
    .Dout(Minute_affichage[3]), .Eout(Minute_affichage[4]), .Fout(Minute_affichage[5]),
    .Gout(Minute_affichage[6]), .Activation(Fuseau_horaire_in[1]));
  Affichage_ville_3 Affichage_ville_3_1 (
    .Choix_ville(Encodeur_choix_Ville_1_output_bus_1), .HorlogeA(Convertisseur_2_a),
    .Aout(Seconde_10_affichage[0]), .HorlogeB(Convertisseur_2_b), .Bout(Seconde_10_affichage[1]),
    .HorlogeC(Convertisseur_2_c), .Cout(Seconde_10_affichage[2]), .HorlogeD(Convertisseur_2_d),
    .Dout(Seconde_10_affichage[3]), .HorlogeE(Convertisseur_2_e), .Eout(Seconde_10_affichage[4]),
    .HorlogeF(Convertisseur_2_f), .Fout(Seconde_10_affichage[5]), .HorlogeG(Convertisseur_2_g),
    .Gout(Seconde_10_affichage[6]), .Activation(Fuseau_horaire_in[1]));
  Affichage_ville_4 Affichage_ville_4_1 (
    .Choix_ville(Encodeur_choix_Ville_1_output_bus_1), .HorlogeA(Convertisseur_1_a),
    .Aout(Seconde_affichage[0]), .HorlogeB(Convertisseur_1_b), .Bout(Seconde_affichage[1]),
    .HorlogeC(Convertisseur_1_c), .Cout(Seconde_affichage[2]), .HorlogeD(Convertisseur_1_d),
    .Dout(Seconde_affichage[3]), .HorlogeE(Convertisseur_1_e), .Eout(Seconde_affichage[4]),
    .HorlogeF(Convertisseur_1_f), .Fout(Seconde_affichage[5]), .HorlogeG(Convertisseur_1_g),
    .Gout(Seconde_affichage[6]), .Activation(Fuseau_horaire_in[1]));

  // Notes on the sheet:
  //   s1_Stopwatch
  //   s2_Stopwatch
  //   m1_Stopwatch
  //   m2_Stopwatch
  //   h1_Stopwatch
  //   h2_Stopwatch
  //   Reset_Fuseau_horaire
  //   Activation_Fuseau_horaire
  //   Bouton_Action_Fuseau_horaire
endmodule

module Set_Digits (
  input  activation,
  input  Set_digit,
  input  s1_in,
  input  s2_in,
  input  m1_in,
  input  m2_in,
  input  h1_in,
  input  h2_in,
  input  reset_digit,
  output [4:0] s1,
  output [4:0] s2,
  output [4:0] m1,
  output [4:0] m2,
  output [4:0] h1,
  output [4:0] h2
);

  wire and_1_out, and_2_out, and_3_out, and_4_out, and_5_out, and_6_out, and_7_out;

  and and_1 (and_1_out, activation, Set_digit);
  and and_2 (and_2_out, activation, s1_in);
  and and_3 (and_3_out, activation, s2_in);
  and and_4 (and_4_out, activation, m1_in);
  and and_5 (and_5_out, activation, m2_in);
  and and_6 (and_6_out, activation, h1_in);
  and and_7 (and_7_out, activation, h2_in);
  DS_manager DS_manager_1 (
    .s1_in(and_2_out), .s2_in(and_3_out), .m1_in(and_4_out), .m2_in(and_5_out), .h1_in(and_6_out),
    .h2_in(and_7_out), .S1(s1[0]), .S2(s2[0]), .S3(m1[0]), .S4(m2[0]), .S5(h1[0]), .S6(h2[0]));
  set_digit_unit set_digit_unit_1 (
    .change(s1[0]), .Button(and_1_out), .Reset(reset_digit), .D3(s1[1]), .D2(s1[2]), .D1(s1[3]), .D0(s1[4]));
  set_digit_dec set_digit_2_1 (
    .Change(s2[0]), .Button(and_1_out), .Reset(reset_digit), .D2(s2[2]), .D1(s2[3]), .D0(s2[4]));
  set_digit_unit set_digit_unit_2 (
    .change(m1[0]), .Button(and_1_out), .Reset(reset_digit), .D3(m1[1]), .D2(m1[2]), .D1(m1[3]), .D0(m1[4]));
  set_digit_dec set_digit_dec_1 (
    .Change(m2[0]), .Button(and_1_out), .Reset(reset_digit), .D2(m2[2]), .D1(m2[3]), .D0(m2[4]));
  set_digit_unit_hour set_digit_5_1 (
    .Change(h1[0]), .Button(and_1_out), .Reset(reset_digit), .Mode(h2[3]), .D3(h1[1]), .D2(h1[2]),
    .D1(h1[3]), .D0(h1[4]));
  set_digit_dec_hour set_digit_6_1 (.Change(h2[0]), .Button(and_1_out), .Reset(reset_digit), .D1(h2[3]), .D0(h2[4]));

  assign h2[2:1] = 2'b00;
  assign m2[1] = 1'b0;
  assign s2[1] = 1'b0;
endmodule

module set_digit_unit (
  input  change,
  input  Button,
  input  Reset,
  output D3,
  output D2,
  output D1,
  output D0
);

  wire Additionneur_1_carry_out, Additionneur_1_resultat, Additionneur_2_carry_out, Additionneur_2_resultat,
       Additionneur_3_carry_out, Additionneur_3_resultat, Additionneur_4_resultat, and_1_out, and_2_out,
       and_3_out, and_4_out, and_5_out, and_6_out, clock_1_out, or_1_out;

  and and_1 (and_1_out, change, Button);
  or or_1 (or_1_out, Reset, and_2_out);
  Clock #(.highDuration(640), .lowDuration(640)) clock_1 (.out(clock_1_out));
  Ajouteur_0a5b1135 Additionneur_1 (
    .a(D0), .b(and_1_out), .carry_in(1'b0), .resultat(Additionneur_1_resultat),
    .carry_out(Additionneur_1_carry_out));
  D_Flip_Flop d_ff_1 (.D(Additionneur_1_resultat), .clk(clock_1_out), .Q(D0), .reset(or_1_out));  // open: Qn, preset
  Ajouteur_0a5b1135 Additionneur_2 (
    .a(D1), .b(Additionneur_1_carry_out), .carry_in(1'b0), .resultat(Additionneur_2_resultat),
    .carry_out(Additionneur_2_carry_out));
  D_Flip_Flop d_ff_2 (.D(Additionneur_2_resultat), .clk(clock_1_out), .Q(D1), .reset(or_1_out));  // open: Qn, preset
  Ajouteur_0a5b1135 Additionneur_3 (
    .a(D2), .b(Additionneur_2_carry_out), .carry_in(1'b0), .resultat(Additionneur_3_resultat),
    .carry_out(Additionneur_3_carry_out));
  D_Flip_Flop d_ff_3 (.D(Additionneur_3_resultat), .clk(clock_1_out), .Q(D2), .reset(or_1_out));  // open: Qn, preset
  and and_2 (and_2_out, and_4_out, and_5_out, and_3_out, and_6_out);
  and and_3 (and_3_out, ~D2, ~1'b0);  // AND_Gate
  and and_4 (and_4_out, ~D0, ~1'b0);  // AND_Gate
  and and_5 (and_5_out, D1, 1'b1);
  and and_6 (and_6_out, D3, 1'b1);
  Ajouteur_0a5b1135 Additionneur_4 (
    .a(D3), .b(Additionneur_3_carry_out), .carry_in(1'b0), .resultat(Additionneur_4_resultat));  // open: carry_out
  D_Flip_Flop d_ff_4 (.D(Additionneur_4_resultat), .clk(clock_1_out), .Q(D3), .reset(or_1_out));  // open: Qn, preset
endmodule

module set_digit_dec (
  input  Change,
  input  Button,
  input  Reset,
  output D2,
  output D1,
  output D0
);

  wire Additionneur_1_carry_out, Additionneur_1_resultat, Additionneur_2_carry_out, Additionneur_2_resultat,
       Additionneur_3_resultat, and_1_out, and_2_out, and_3_out, and_4_out, and_5_out, clock_1_out, or_1_out;

  and and_1 (and_1_out, Change, Button);
  or or_1 (or_1_out, Reset, and_2_out);
  Clock #(.highDuration(640), .lowDuration(640)) clock_1 (.out(clock_1_out));
  Ajouteur_0a5b1135 Additionneur_1 (
    .a(D0), .b(and_1_out), .carry_in(1'b0), .resultat(Additionneur_1_resultat),
    .carry_out(Additionneur_1_carry_out));
  D_Flip_Flop d_ff_1 (.D(Additionneur_1_resultat), .clk(clock_1_out), .Q(D0), .reset(or_1_out));  // open: Qn, preset
  Ajouteur_0a5b1135 Additionneur_2 (
    .a(D1), .b(Additionneur_1_carry_out), .carry_in(1'b0), .resultat(Additionneur_2_resultat),
    .carry_out(Additionneur_2_carry_out));
  D_Flip_Flop d_ff_2 (.D(Additionneur_2_resultat), .clk(clock_1_out), .Q(D1), .reset(or_1_out));  // open: Qn, preset
  and and_2 (and_2_out, and_3_out, and_4_out, and_5_out);
  Ajouteur_0a5b1135 Additionneur_3 (
    .a(D2), .b(Additionneur_2_carry_out), .carry_in(1'b0), .resultat(Additionneur_3_resultat));  // open: carry_out
  D_Flip_Flop d_ff_3 (.D(Additionneur_3_resultat), .clk(clock_1_out), .Q(D2), .reset(or_1_out));  // open: Qn, preset
  and and_3 (and_3_out, ~D0, ~1'b0);  // AND_Gate
  and and_4 (and_4_out, D1, 1'b1);
  and and_5 (and_5_out, D2, 1'b1);
endmodule

module set_digit_unit_hour (
  input  Change,
  input  Button,
  input  Reset,
  input  Mode,
  output D3,
  output D2,
  output D1,
  output D0
);

  wire Additionneur_1_carry_out, Additionneur_1_resultat, Additionneur_2_carry_out, Additionneur_2_resultat,
       Additionneur_3_carry_out, Additionneur_3_resultat, Additionneur_4_resultat, and_1_out, and_2_out,
       and_3_out, and_4_out, and_5_out, and_6_out, clock_1_out, nand_1_out, nand_2_out, nand_3_out, or_1_out;

  and and_1 (and_1_out, Change, Button);
  or or_1 (or_1_out, Reset, nand_1_out, and_2_out);
  Clock #(.highDuration(640), .lowDuration(640)) clock_1 (.out(clock_1_out));
  nand nand_1 (nand_1_out, nand_2_out, nand_3_out);
  nand nand_2 (nand_2_out, Mode, D3);
  nand nand_3 (nand_3_out, Mode, D2);
  Ajouteur_0a5b1135 Additionneur_1 (
    .a(D0), .b(and_1_out), .carry_in(1'b0), .resultat(Additionneur_1_resultat),
    .carry_out(Additionneur_1_carry_out));
  D_Flip_Flop d_ff_1 (.D(Additionneur_1_resultat), .clk(clock_1_out), .Q(D0), .reset(or_1_out));  // open: Qn, preset
  and and_2 (and_2_out, and_3_out, and_4_out, and_5_out, and_6_out);
  and and_3 (and_3_out, ~D0, ~1'b0);  // AND_Gate
  and and_4 (and_4_out, D1, 1'b1);
  and and_5 (and_5_out, ~D2, ~1'b0);  // AND_Gate
  and and_6 (and_6_out, D3, 1'b1);
  Ajouteur_0a5b1135 Additionneur_2 (
    .a(D1), .b(Additionneur_1_carry_out), .carry_in(1'b0), .resultat(Additionneur_2_resultat),
    .carry_out(Additionneur_2_carry_out));
  D_Flip_Flop d_ff_2 (.D(Additionneur_2_resultat), .clk(clock_1_out), .Q(D1), .reset(or_1_out));  // open: Qn, preset
  Ajouteur_0a5b1135 Additionneur_3 (
    .a(D2), .b(Additionneur_2_carry_out), .carry_in(1'b0), .resultat(Additionneur_3_resultat),
    .carry_out(Additionneur_3_carry_out));
  D_Flip_Flop d_ff_3 (.D(Additionneur_3_resultat), .clk(clock_1_out), .Q(D2), .reset(or_1_out));  // open: Qn, preset
  Ajouteur_0a5b1135 Additionneur_4 (
    .a(D3), .b(Additionneur_3_carry_out), .carry_in(1'b0), .resultat(Additionneur_4_resultat));  // open: carry_out
  D_Flip_Flop d_ff_4 (.D(Additionneur_4_resultat), .clk(clock_1_out), .Q(D3), .reset(or_1_out));  // open: Qn, preset
endmodule

module set_digit_dec_hour (
  input  Change,
  input  Button,
  input  Reset,
  output D1,
  output D0
);

  wire Additionneur_1_carry_out, Additionneur_1_resultat, Additionneur_2_resultat, and_1_out, and_2_out,
       clock_1_out, or_1_out;

  and and_1 (and_1_out, Change, Button);
  or or_1 (or_1_out, Reset, and_2_out);
  Clock #(.highDuration(640), .lowDuration(640)) clock_1 (.out(clock_1_out));
  Ajouteur_0a5b1135 Additionneur_1 (
    .a(D0), .b(and_1_out), .carry_in(1'b0), .resultat(Additionneur_1_resultat),
    .carry_out(Additionneur_1_carry_out));
  D_Flip_Flop d_ff_1 (.D(Additionneur_1_resultat), .clk(clock_1_out), .Q(D0), .reset(or_1_out));  // open: Qn, preset
  and and_2 (and_2_out, D0, D1);
  Ajouteur_0a5b1135 Additionneur_2 (
    .a(D1), .b(Additionneur_1_carry_out), .carry_in(1'b0), .resultat(Additionneur_2_resultat));  // open: carry_out
  D_Flip_Flop d_ff_2 (.D(Additionneur_2_resultat), .clk(clock_1_out), .Q(D1), .reset(or_1_out));  // open: Qn, preset
endmodule

module All_digit_checker (
  input  Alarm_activation,
  input  [4:0] A_Digit_1,
  input  [4:0] B_Digit_1,
  input  [4:0] A_Digit_2,
  input  [4:0] B_Digit_2,
  input  [4:0] A_Digit_3,
  input  [4:0] B_Digit_3,
  input  [4:0] A_Digit_4,
  input  [4:0] B_Digit_4,
  input  [4:0] A_Digit_5,
  input  [4:0] B_Digit_5,
  input  [4:0] A_Digit_6,
  input  [4:0] B_Digit_6,
  output BEEP_BEEP
);

  wire digit_checker_1_alarm, digit_checker_2_alarm, digit_checker_3_alarm, digit_checker_4_alarm,
       digit_checker_5_alarm, digit_checker_6_alarm;

  digit_checker digit_checker_1 (
    .A3(A_Digit_1[1]), .B3(B_Digit_1[1]), .A2(A_Digit_1[2]), .B2(B_Digit_1[2]), .A1(A_Digit_1[3]),
    .B1(B_Digit_1[3]), .A0(A_Digit_1[4]), .B0(B_Digit_1[4]), .alarm(digit_checker_1_alarm));
  digit_checker digit_checker_2 (
    .A3(A_Digit_2[1]), .B3(B_Digit_2[1]), .A2(A_Digit_2[2]), .B2(B_Digit_2[2]), .A1(A_Digit_2[3]),
    .B1(B_Digit_2[3]), .A0(A_Digit_2[4]), .B0(B_Digit_2[4]), .alarm(digit_checker_2_alarm));
  digit_checker digit_checker_3 (
    .A3(A_Digit_3[1]), .B3(B_Digit_3[1]), .A2(A_Digit_3[2]), .B2(B_Digit_3[2]), .A1(A_Digit_3[3]),
    .B1(B_Digit_3[3]), .A0(A_Digit_3[4]), .B0(B_Digit_3[4]), .alarm(digit_checker_3_alarm));
  digit_checker digit_checker_4 (
    .A3(A_Digit_4[1]), .B3(B_Digit_4[1]), .A2(A_Digit_4[2]), .B2(B_Digit_4[2]), .A1(A_Digit_4[3]),
    .B1(B_Digit_4[3]), .A0(A_Digit_4[4]), .B0(B_Digit_4[4]), .alarm(digit_checker_4_alarm));
  digit_checker digit_checker_5 (
    .A3(A_Digit_5[1]), .B3(B_Digit_5[1]), .A2(A_Digit_5[2]), .B2(B_Digit_5[2]), .A1(A_Digit_5[3]),
    .B1(B_Digit_5[3]), .A0(A_Digit_5[4]), .B0(B_Digit_5[4]), .alarm(digit_checker_5_alarm));
  digit_checker digit_checker_6 (
    .A3(A_Digit_6[1]), .B3(B_Digit_6[1]), .A2(A_Digit_6[2]), .B2(B_Digit_6[2]), .A1(A_Digit_6[3]),
    .B1(B_Digit_6[3]), .A0(A_Digit_6[4]), .B0(B_Digit_6[4]), .alarm(digit_checker_6_alarm));
  and and_1 (BEEP_BEEP, digit_checker_1_alarm, digit_checker_2_alarm, digit_checker_3_alarm, Alarm_activation, digit_checker_4_alarm, digit_checker_5_alarm, digit_checker_6_alarm);
endmodule

module digit_checker (
  input  A3,
  input  B3,
  input  A2,
  input  B2,
  input  A1,
  input  B1,
  input  A0,
  input  B0,
  output alarm
);

  wire xnor_1_out, xnor_2_out, xnor_3_out, xnor_4_out;

  xnor xnor_1 (xnor_1_out, A3, B3);
  xnor xnor_2 (xnor_2_out, A2, B2);
  xnor xnor_3 (xnor_3_out, A1, B1);
  xnor xnor_4 (xnor_4_out, A0, B0);
  and and_1 (alarm, xnor_1_out, xnor_2_out, xnor_3_out, xnor_4_out);
endmodule

module Alarm (
  input  [9:0] Alarm_in,
  input  [29:0] Horloge_in,
  output [29:0] Alarm_out,
  output BEEP_BEEP
);

  wire clock_1_out, Detecteur_flanc_montant_1_sortie, s_r_ff_1_q;

  Detecteur_flanc_montant Detecteur_flanc_montant_1 (.Entree(Alarm_in[2]), .Sortie(Detecteur_flanc_montant_1_sortie));
  Clock clock_1 (.out(clock_1_out));
  S_R_Flip_Flop s_r_ff_1 (
    .clk(clock_1_out), .Q(s_r_ff_1_q), .reset(Alarm_in[9]), .preset(Alarm_in[0]));  // open: S, R, Qn
  Set_Digits Set_Digits_1 (
    .activation(Alarm_in[1]), .Set_digit(Detecteur_flanc_montant_1_sortie), .s1_in(Alarm_in[3]),
    .s2_in(Alarm_in[4]), .m1_in(Alarm_in[5]), .m2_in(Alarm_in[6]), .h1_in(Alarm_in[7]), .h2_in(Alarm_in[8]),
    .reset_digit(Alarm_in[9]), .s1(Alarm_out[4:0]), .s2(Alarm_out[9:5]), .m1(Alarm_out[14:10]),
    .m2(Alarm_out[19:15]), .h1(Alarm_out[24:20]), .h2(Alarm_out[29:25]));
  All_digit_checker All_digit_checker_1 (
    .Alarm_activation(s_r_ff_1_q), .A_Digit_1(Alarm_out[4:0]), .B_Digit_1(Horloge_in[4:0]),
    .A_Digit_2(Alarm_out[9:5]), .B_Digit_2(Horloge_in[9:5]), .A_Digit_3(Alarm_out[14:10]),
    .B_Digit_3(Horloge_in[14:10]), .A_Digit_4(Alarm_out[19:15]), .B_Digit_4(Horloge_in[19:15]),
    .A_Digit_5(Alarm_out[24:20]), .B_Digit_5(Horloge_in[24:20]), .A_Digit_6(Alarm_out[29:25]),
    .B_Digit_6(Horloge_in[29:25]), .BEEP_BEEP(BEEP_BEEP));

  // Notes on the sheet:
  //   Stand_by_Alarm
  //   mode_Alarm
  //   Set_digit_Alarm
  //   set_s1_Alarm
  //   set_s2_Alarm
  //   set_m1_Alarm
  //   set_m2_Alarm
  //   set_h1_Alarm
  //   set_h2_Alarm
  //   reset_Alarm
  //   s1_Horloge
  //   s2_Horloge
  //   m1_Horloge
  //   m2_Horloge
  //   h1_Horloge
  //   h2_Horloge
  //   s1
  //   s2
  //   m1
  //   m2
  //   h1
  //   h2
endmodule

module DS_manager (
  input  s1_in,
  input  s2_in,
  input  m1_in,
  input  m2_in,
  input  h1_in,
  input  h2_in,
  output S1,
  output S2,
  output S3,
  output S4,
  output S5,
  output S6
);

  wire not_1_out, not_2_out, not_3_out, not_4_out, not_5_out, not_6_out, not_7_out, not_8_out, not_9_out,
       not_10_out, not_11_out, not_12_out, not_13_out, not_14_out, not_15_out;

  not not_1 (not_1_out, s2_in);
  not not_2 (not_2_out, m1_in);
  not not_3 (not_3_out, m2_in);
  not not_4 (not_4_out, h1_in);
  not not_5 (not_5_out, h2_in);
  not not_6 (not_6_out, m1_in);
  not not_7 (not_7_out, m2_in);
  not not_8 (not_8_out, h1_in);
  not not_9 (not_9_out, h2_in);
  not not_10 (not_10_out, m2_in);
  not not_11 (not_11_out, h1_in);
  not not_12 (not_12_out, h2_in);
  not not_13 (not_13_out, h1_in);
  not not_14 (not_14_out, h2_in);
  not not_15 (not_15_out, h2_in);
  and and_1 (S1, s1_in, not_1_out, not_2_out, not_3_out, not_4_out, not_5_out);
  and and_2 (S2, s2_in, not_6_out, not_7_out, not_8_out, not_9_out);
  and and_3 (S3, m1_in, not_10_out, not_11_out, not_12_out);
  and and_4 (S4, m2_in, not_13_out, not_14_out);
  and and_5 (S5, h1_in, not_15_out);

  assign S6 = h2_in;
endmodule

module Ajouteur_0a5b1135 (
  input  a,
  input  b,
  input  carry_in,
  output resultat,
  output carry_out
);

  wire nand_1_out, nand_2_out, nand_3_out, nand_4_out, nand_5_out, nand_6_out, nand_7_out, nand_8_out,
       nand_9_out, nand_10_out, nand_11_out, nand_12_out, nand_13_out;

  nand nand_1 (nand_1_out, a, a);
  nand nand_2 (nand_2_out, b, b);
  nand nand_3 (nand_3_out, a, a);
  nand nand_4 (nand_4_out, carry_in, carry_in);
  nand nand_5 (nand_5_out, b, b);
  nand nand_6 (nand_6_out, carry_in, carry_in);
  nand nand_7 (nand_7_out, b, carry_in);
  nand nand_8 (nand_8_out, a, carry_in);
  nand nand_9 (nand_9_out, a, b);
  nand nand_10 (nand_10_out, nand_1_out, nand_2_out, carry_in);
  nand nand_11 (nand_11_out, nand_3_out, b, nand_4_out);
  nand nand_12 (nand_12_out, a, nand_5_out, nand_6_out);
  nand nand_13 (nand_13_out, a, b, carry_in);
  nand nand_14 (carry_out, nand_7_out, nand_8_out, nand_9_out);
  nand nand_15 (resultat, nand_10_out, nand_11_out, nand_12_out, nand_13_out);
endmodule

module Select_mode (
  input  B_mode,
  input  Reset,
  output [2:0] Mode
);

  wire Additionneur_1_carry_out, Additionneur_1_resultat, Additionneur_2_carry_out, Additionneur_2_resultat,
       Additionneur_3_resultat, and_1_out, clock_1_out, or_1_out;

  Clock #(.highDuration(14000), .lowDuration(14000)) clock_1 (.out(clock_1_out));
  Ajouteur_0a5b1135 Additionneur_1 (
    .a(Mode[0]), .b(B_mode), .carry_in(1'b0), .resultat(Additionneur_1_resultat),
    .carry_out(Additionneur_1_carry_out));
  D_Flip_Flop d_ff_1 (
    .D(Additionneur_1_resultat), .clk(clock_1_out), .Q(Mode[0]), .reset(or_1_out));  // open: Qn, preset
  Ajouteur_0a5b1135 Additionneur_2 (
    .a(Mode[1]), .b(Additionneur_1_carry_out), .carry_in(1'b0), .resultat(Additionneur_2_resultat),
    .carry_out(Additionneur_2_carry_out));
  D_Flip_Flop d_ff_2 (
    .D(Additionneur_2_resultat), .clk(clock_1_out), .Q(Mode[1]), .reset(or_1_out));  // open: Qn, preset
  or or_1 (or_1_out, Reset, and_1_out);
  Ajouteur_0a5b1135 Additionneur_3 (
    .a(Mode[2]), .b(Additionneur_2_carry_out), .carry_in(1'b0), .resultat(Additionneur_3_resultat));  // open: carry_out
  D_Flip_Flop d_ff_3 (
    .D(Additionneur_3_resultat), .clk(clock_1_out), .Q(Mode[2]), .reset(or_1_out));  // open: Qn, preset
  and and_1 (and_1_out, Mode[0], ~Mode[1], Mode[2]);  // AND_Gate
endmodule

module Notes_Musique_1 (
  input  B_1,
  input  B_2,
  input  E_1,
  input  E_2,
  input  E_3,
  input  G_1,
  input  F_1,
  input  F_2,
  input  E_4,
  input  E_5,
  input  E_6,
  input  E_7,
  input  B2_1,
  input  B2_2,
  input  A2_1,
  input  A2_2,
  input  A2_3,
  input  A2_4,
  input  A2_5,
  input  Fs_1,
  input  Fs_2,
  input  Fs_3,
  input  Fs_4,
  input  Fs_5,
  input  E_8,
  input  E_9,
  input  E_10,
  input  G_2,
  input  F_3,
  input  F_4,
  input  Ds_1,
  input  Ds_2,
  output B_1_out,
  output B_2_out,
  output E_1_out,
  output E_2_out,
  output E_3_out,
  output G_1_out,
  output F_1_out,
  output F_2_out,
  output E_4_out,
  output E_5_out,
  output E_6_out,
  output E_7_out,
  output B2_1_out,
  output B2_2_out,
  output A2_1_out,
  output A2_2_out,
  output A2_3_out,
  output A2_4_out,
  output A2_5_out,
  output Fs_1_out,
  output Fs_2_out,
  output Fs_3_out,
  output Fs_4_out,
  output Fs_5_out,
  output E_8_out,
  output E_9_out,
  output E_10_out,
  output G_2_out,
  output F_3_out,
  output F_4_out,
  output Ds_1_out,
  output Ds_2_out
);

  wire Clock_A2_out, Clock_B2_out, Clock_B_out, Clock_Ds_out, Clock_E_out, Clock_F_out, Clock_Fs_out,
       Clock_G_out;

  Clock #(.highDuration(104), .lowDuration(104)) Clock_B (.out(Clock_B_out));
  Clock #(.highDuration(78), .lowDuration(78)) Clock_E (.out(Clock_E_out));
  Clock #(.highDuration(65), .lowDuration(65)) Clock_G (.out(Clock_G_out));
  Clock #(.highDuration(73), .lowDuration(73)) Clock_F (.out(Clock_F_out));
  Clock #(.highDuration(52), .lowDuration(52)) Clock_B2 (.out(Clock_B2_out));
  Clock #(.highDuration(58), .lowDuration(58)) Clock_A2 (.out(Clock_A2_out));
  Clock #(.highDuration(69), .lowDuration(69)) Clock_Fs (.out(Clock_Fs_out));
  Clock #(.highDuration(82), .lowDuration(82)) Clock_Ds (.out(Clock_Ds_out));
  and and_1 (B_1_out, B_1, Clock_B_out);
  and and_2 (B_2_out, B_2, Clock_B_out);
  and and_3 (E_1_out, E_1, Clock_E_out);
  and and_4 (E_2_out, E_2, Clock_E_out);
  and and_5 (E_3_out, E_3, Clock_E_out);
  and and_6 (G_1_out, G_1, Clock_G_out);
  and and_7 (F_1_out, F_1, Clock_F_out);
  and and_8 (F_2_out, F_2, Clock_F_out);
  and and_9 (E_4_out, E_4, Clock_E_out);
  and and_10 (E_5_out, E_5, Clock_E_out);
  and and_11 (E_6_out, E_6, Clock_E_out);
  and and_12 (E_7_out, E_7, Clock_E_out);
  and and_13 (B2_1_out, B2_1, Clock_B2_out);
  and and_14 (B2_2_out, B2_2, Clock_B2_out);
  and and_15 (A2_1_out, A2_1, Clock_A2_out);
  and and_16 (A2_2_out, A2_2, Clock_A2_out);
  and and_17 (A2_3_out, A2_3, Clock_A2_out);
  and and_18 (A2_4_out, A2_4, Clock_A2_out);
  and and_19 (A2_5_out, A2_5, Clock_A2_out);
  and and_20 (Fs_1_out, Fs_1, Clock_Fs_out);
  and and_21 (Fs_2_out, Fs_2, Clock_Fs_out);
  and and_22 (Fs_3_out, Fs_3, Clock_Fs_out);
  and and_23 (Fs_4_out, Fs_4, Clock_Fs_out);
  and and_24 (Fs_5_out, Fs_5, Clock_Fs_out);
  and and_25 (E_8_out, E_8, Clock_E_out);
  and and_26 (E_9_out, E_9, Clock_E_out);
  and and_27 (E_10_out, E_10, Clock_E_out);
  and and_28 (G_2_out, G_2, Clock_G_out);
  and and_29 (F_3_out, F_3, Clock_F_out);
  and and_30 (F_4_out, F_4, Clock_F_out);
  and and_31 (Ds_1_out, Ds_1, Clock_Ds_out);
  and and_32 (Ds_2_out, Ds_2, Clock_Ds_out);
endmodule

module Notes_musique_2 (
  input  Ds_3,
  input  Ds_4,
  input  F_5,
  input  F_6,
  input  B_3,
  input  B_4,
  input  B_5,
  input  B_6,
  input  B_7,
  output Ds_3_out,
  output Ds_4_out,
  output F_5_out,
  output F_6_out,
  output B_3_out,
  output B_4_out,
  output B_5_out,
  output B_6_out,
  output B_7_out
);

  wire Clock_B_out, Clock_Ds_out, Clock_F_out;

  Clock #(.highDuration(82), .lowDuration(82)) Clock_Ds (.out(Clock_Ds_out));
  Clock #(.highDuration(73), .lowDuration(73)) Clock_F (.out(Clock_F_out));
  Clock #(.highDuration(104), .lowDuration(104)) Clock_B (.out(Clock_B_out));
  and and_1 (Ds_3_out, Ds_3, Clock_Ds_out);
  and and_2 (Ds_4_out, Ds_4, Clock_Ds_out);
  and and_3 (F_5_out, F_5, Clock_F_out);
  and and_4 (F_6_out, F_6, Clock_F_out);
  and and_5 (B_3_out, B_3, Clock_B_out);
  and and_6 (B_4_out, B_4, Clock_B_out);
  and and_7 (B_5_out, B_5, Clock_B_out);
  and and_8 (B_6_out, B_6, Clock_B_out);
  and and_9 (B_7_out, B_7, Clock_B_out);
endmodule

module Harry_Potter (
  input  BEEP_BEEP,
  input  Stop,
  output Musique,
  output Terre
);

  wire and_1_out, and_2_out, and_3_out, and_4_out, and_5_out, and_6_out, and_7_out, and_8_out, and_9_out,
       and_10_out, and_11_out, clock_1_out, clock_2_out, demultiplexer_1_out0, demultiplexer_1_out1,
       demultiplexer_1_out2, demultiplexer_1_out3, demultiplexer_1_out4, demultiplexer_1_out5,
       demultiplexer_1_out6, demultiplexer_1_out7, demultiplexer_1_out8, demultiplexer_1_out9,
       demultiplexer_1_out10, demultiplexer_1_out11, demultiplexer_1_out12, demultiplexer_1_out13,
       demultiplexer_1_out14, demultiplexer_1_out15, demultiplexer_1_out16, demultiplexer_1_out17,
       demultiplexer_1_out18, demultiplexer_1_out19, demultiplexer_1_out20, demultiplexer_1_out21,
       demultiplexer_1_out22, demultiplexer_1_out23, demultiplexer_1_out24, demultiplexer_1_out25,
       demultiplexer_1_out26, demultiplexer_1_out27, demultiplexer_1_out28, demultiplexer_1_out29,
       demultiplexer_1_out30, demultiplexer_1_out31, demultiplexer_2_out0, demultiplexer_2_out1,
       demultiplexer_2_out2, demultiplexer_2_out3, demultiplexer_2_out4, demultiplexer_2_out5,
       demultiplexer_2_out6, demultiplexer_2_out7, demultiplexer_2_out8, demultiplexer_2_out9,
       demultiplexer_2_out10, demultiplexer_2_out11, demultiplexer_2_out12, demultiplexer_2_out13,
       demultiplexer_2_out14, demultiplexer_2_out15, multiplexer_1_out, multiplexer_2_out, not_1_out,
       Notes_Musique_1_1_a2_1_out, Notes_Musique_1_1_a2_2_out, Notes_Musique_1_1_a2_3_out,
       Notes_Musique_1_1_a2_4_out, Notes_Musique_1_1_a2_5_out, Notes_Musique_1_1_b2_1_out,
       Notes_Musique_1_1_b2_2_out, Notes_Musique_1_1_b_1_out, Notes_Musique_1_1_b_2_out,
       Notes_Musique_1_1_ds_1_out, Notes_Musique_1_1_ds_2_out, Notes_Musique_1_1_e_1_out,
       Notes_Musique_1_1_e_2_out, Notes_Musique_1_1_e_3_out, Notes_Musique_1_1_e_4_out,
       Notes_Musique_1_1_e_5_out, Notes_Musique_1_1_e_6_out, Notes_Musique_1_1_e_7_out,
       Notes_Musique_1_1_e_8_out, Notes_Musique_1_1_e_9_out, Notes_Musique_1_1_e_10_out,
       Notes_Musique_1_1_f_1_out, Notes_Musique_1_1_f_2_out, Notes_Musique_1_1_f_3_out,
       Notes_Musique_1_1_f_4_out, Notes_Musique_1_1_fs_1_out, Notes_Musique_1_1_fs_2_out,
       Notes_Musique_1_1_fs_3_out, Notes_Musique_1_1_fs_4_out, Notes_Musique_1_1_fs_5_out,
       Notes_Musique_1_1_g_1_out, Notes_Musique_1_1_g_2_out, Notes_musique_2_1_b_3_out,
       Notes_musique_2_1_b_4_out, Notes_musique_2_1_b_5_out, Notes_musique_2_1_b_6_out,
       Notes_musique_2_1_b_7_out, Notes_musique_2_1_ds_3_out, Notes_musique_2_1_ds_4_out,
       Notes_musique_2_1_f_5_out, Notes_musique_2_1_f_6_out, or_1_out, or_2_out, or_3_out, s_r_ff_1_q;
  wire [3:0] t_ff_1_q;
  wire [4:0] t_ff_5_q;

  S_R_Flip_Flop s_r_ff_1 (.clk(clock_1_out), .Q(s_r_ff_1_q), .reset(Stop), .preset(BEEP_BEEP));  // open: S, R, Qn
  Clock clock_1 (.out(clock_1_out));
  and and_1 (and_1_out, s_r_ff_1_q, ~demultiplexer_1_out31);  // AND_Gate
  and and_2 (and_2_out, demultiplexer_1_out31, ~and_1_out);  // AND_Gate
  or or_1 (or_1_out, Stop, or_3_out);
  Clock #(.highDuration(25600)) clock_2 (.out(clock_2_out));
  or or_2 (or_2_out, Stop, or_3_out);
  and and_3 (and_3_out, t_ff_5_q[0], and_1_out);
  and and_4 (and_4_out, t_ff_5_q[1], t_ff_5_q[0], and_1_out);
  and and_5 (and_5_out, t_ff_5_q[2], t_ff_5_q[1], t_ff_5_q[0], and_1_out);
  and and_6 (and_6_out, t_ff_5_q[3], t_ff_5_q[2], t_ff_5_q[1], t_ff_5_q[0], and_1_out);
  T_Flip_Flop t_ff_1 (.T(and_2_out), .clk(clock_2_out), .Q(t_ff_1_q[0]), .reset(or_1_out));  // open: Qn, preset
  T_Flip_Flop t_ff_2 (.T(and_7_out), .clk(clock_2_out), .Q(t_ff_1_q[1]), .reset(or_1_out));  // open: Qn, preset
  and and_7 (and_7_out, t_ff_1_q[0], and_2_out);
  T_Flip_Flop t_ff_3 (.T(and_8_out), .clk(clock_2_out), .Q(t_ff_1_q[2]), .reset(or_1_out));  // open: Qn, preset
  and and_8 (and_8_out, t_ff_1_q[1], t_ff_1_q[0], and_2_out);
  T_Flip_Flop t_ff_4 (.T(and_9_out), .clk(clock_2_out), .Q(t_ff_1_q[3]), .reset(or_1_out));  // open: Qn, preset
  and and_9 (and_9_out, t_ff_1_q[2], t_ff_1_q[1], t_ff_1_q[0], and_2_out);
  T_Flip_Flop t_ff_5 (.T(and_1_out), .clk(clock_2_out), .Q(t_ff_5_q[0]), .reset(or_2_out));  // open: Qn, preset
  T_Flip_Flop t_ff_6 (.T(and_3_out), .clk(clock_2_out), .Q(t_ff_5_q[1]), .reset(or_2_out));  // open: Qn, preset
  T_Flip_Flop t_ff_7 (.T(and_4_out), .clk(clock_2_out), .Q(t_ff_5_q[2]), .reset(or_2_out));  // open: Qn, preset
  T_Flip_Flop t_ff_8 (.T(and_5_out), .clk(clock_2_out), .Q(t_ff_5_q[3]), .reset(or_2_out));  // open: Qn, preset
  T_Flip_Flop t_ff_9 (.T(and_6_out), .clk(clock_2_out), .Q(t_ff_5_q[4]), .reset(or_2_out));  // open: Qn, preset
  Demultiplexer #(.select(5), .enable("false")) demultiplexer_1 (
    .out0(demultiplexer_1_out0), .out1(demultiplexer_1_out1), .out2(demultiplexer_1_out2),
    .out3(demultiplexer_1_out3), .out4(demultiplexer_1_out4), .out5(demultiplexer_1_out5),
    .out6(demultiplexer_1_out6), .out7(demultiplexer_1_out7), .out8(demultiplexer_1_out8),
    .out9(demultiplexer_1_out9), .out10(demultiplexer_1_out10), .out11(demultiplexer_1_out11),
    .out12(demultiplexer_1_out12), .out13(demultiplexer_1_out13), .out14(demultiplexer_1_out14),
    .out15(demultiplexer_1_out15), .out16(demultiplexer_1_out16), .out17(demultiplexer_1_out17),
    .out18(demultiplexer_1_out18), .out19(demultiplexer_1_out19), .out20(demultiplexer_1_out20),
    .out21(demultiplexer_1_out21), .out22(demultiplexer_1_out22), .out23(demultiplexer_1_out23),
    .out24(demultiplexer_1_out24), .out25(demultiplexer_1_out25), .out26(demultiplexer_1_out26),
    .out27(demultiplexer_1_out27), .out28(demultiplexer_1_out28), .out29(demultiplexer_1_out29),
    .out30(demultiplexer_1_out30), .out31(demultiplexer_1_out31), .in(1'b1), .sel(t_ff_5_q));
  Demultiplexer #(.select(4), .enable("false")) demultiplexer_2 (
    .out0(demultiplexer_2_out0), .out1(demultiplexer_2_out1), .out2(demultiplexer_2_out2),
    .out3(demultiplexer_2_out3), .out4(demultiplexer_2_out4), .out5(demultiplexer_2_out5),
    .out6(demultiplexer_2_out6), .out7(demultiplexer_2_out7), .out8(demultiplexer_2_out8),
    .out9(demultiplexer_2_out9), .out10(demultiplexer_2_out10), .out11(demultiplexer_2_out11),
    .out12(demultiplexer_2_out12), .out13(demultiplexer_2_out13), .out14(demultiplexer_2_out14),
    .out15(demultiplexer_2_out15), .in(1'b1), .sel(t_ff_1_q));
  or or_3 (or_3_out, demultiplexer_2_out10, demultiplexer_2_out11, demultiplexer_2_out12, demultiplexer_2_out13, demultiplexer_2_out14, demultiplexer_2_out15);
  Notes_Musique_1 Notes_Musique_1_1 (
    .B_1(demultiplexer_1_out0), .B_2(demultiplexer_1_out1), .E_1(demultiplexer_1_out2),
    .E_2(demultiplexer_1_out3), .E_3(demultiplexer_1_out4), .G_1(demultiplexer_1_out5),
    .F_1(demultiplexer_1_out6), .F_2(demultiplexer_1_out7), .E_4(demultiplexer_1_out8),
    .E_5(demultiplexer_1_out9), .E_6(demultiplexer_1_out10), .E_7(demultiplexer_1_out11),
    .B2_1(demultiplexer_1_out12), .B2_2(demultiplexer_1_out13), .A2_1(demultiplexer_1_out14),
    .A2_2(demultiplexer_1_out15), .A2_3(demultiplexer_1_out16), .A2_4(demultiplexer_1_out17),
    .A2_5(demultiplexer_1_out18), .Fs_1(demultiplexer_1_out19), .Fs_2(demultiplexer_1_out20),
    .Fs_3(demultiplexer_1_out21), .Fs_4(demultiplexer_1_out22), .Fs_5(demultiplexer_1_out23),
    .E_8(demultiplexer_1_out24), .E_9(demultiplexer_1_out25), .E_10(demultiplexer_1_out26),
    .G_2(demultiplexer_1_out27), .F_3(demultiplexer_1_out28), .F_4(demultiplexer_1_out29),
    .Ds_1(demultiplexer_1_out30), .Ds_2(demultiplexer_1_out31), .B_1_out(Notes_Musique_1_1_b_1_out),
    .B_2_out(Notes_Musique_1_1_b_2_out), .E_1_out(Notes_Musique_1_1_e_1_out),
    .E_2_out(Notes_Musique_1_1_e_2_out), .E_3_out(Notes_Musique_1_1_e_3_out),
    .G_1_out(Notes_Musique_1_1_g_1_out), .F_1_out(Notes_Musique_1_1_f_1_out),
    .F_2_out(Notes_Musique_1_1_f_2_out), .E_4_out(Notes_Musique_1_1_e_4_out),
    .E_5_out(Notes_Musique_1_1_e_5_out), .E_6_out(Notes_Musique_1_1_e_6_out),
    .E_7_out(Notes_Musique_1_1_e_7_out), .B2_1_out(Notes_Musique_1_1_b2_1_out),
    .B2_2_out(Notes_Musique_1_1_b2_2_out), .A2_1_out(Notes_Musique_1_1_a2_1_out),
    .A2_2_out(Notes_Musique_1_1_a2_2_out), .A2_3_out(Notes_Musique_1_1_a2_3_out),
    .A2_4_out(Notes_Musique_1_1_a2_4_out), .A2_5_out(Notes_Musique_1_1_a2_5_out),
    .Fs_1_out(Notes_Musique_1_1_fs_1_out), .Fs_2_out(Notes_Musique_1_1_fs_2_out),
    .Fs_3_out(Notes_Musique_1_1_fs_3_out), .Fs_4_out(Notes_Musique_1_1_fs_4_out),
    .Fs_5_out(Notes_Musique_1_1_fs_5_out), .E_8_out(Notes_Musique_1_1_e_8_out),
    .E_9_out(Notes_Musique_1_1_e_9_out), .E_10_out(Notes_Musique_1_1_e_10_out),
    .G_2_out(Notes_Musique_1_1_g_2_out), .F_3_out(Notes_Musique_1_1_f_3_out),
    .F_4_out(Notes_Musique_1_1_f_4_out), .Ds_1_out(Notes_Musique_1_1_ds_1_out),
    .Ds_2_out(Notes_Musique_1_1_ds_2_out));
  Notes_musique_2 Notes_musique_2_1 (
    .Ds_3(demultiplexer_2_out0), .Ds_4(demultiplexer_2_out1), .F_5(demultiplexer_2_out2),
    .F_6(demultiplexer_2_out3), .B_3(demultiplexer_2_out4), .B_4(demultiplexer_2_out5),
    .B_5(demultiplexer_2_out6), .B_6(demultiplexer_2_out7), .B_7(demultiplexer_2_out8),
    .Ds_3_out(Notes_musique_2_1_ds_3_out), .Ds_4_out(Notes_musique_2_1_ds_4_out),
    .F_5_out(Notes_musique_2_1_f_5_out), .F_6_out(Notes_musique_2_1_f_6_out),
    .B_3_out(Notes_musique_2_1_b_3_out), .B_4_out(Notes_musique_2_1_b_4_out),
    .B_5_out(Notes_musique_2_1_b_5_out), .B_6_out(Notes_musique_2_1_b_6_out),
    .B_7_out(Notes_musique_2_1_b_7_out));
  not not_1 (not_1_out, demultiplexer_2_out9);
  Multiplexer #(.select(4), .enable("false")) multiplexer_1 (
    .in0(Notes_musique_2_1_ds_3_out), .in1(Notes_musique_2_1_ds_4_out), .in2(Notes_musique_2_1_f_5_out),
    .in3(Notes_musique_2_1_f_6_out), .in4(Notes_musique_2_1_b_3_out), .in5(Notes_musique_2_1_b_4_out),
    .in6(Notes_musique_2_1_b_5_out), .in7(Notes_musique_2_1_b_6_out), .in8(Notes_musique_2_1_b_7_out),
    .in9(not_1_out), .in10(1'b0), .in11(1'b0), .in12(1'b0), .in13(1'b0), .in14(1'b0), .in15(1'b0),
    .out(multiplexer_1_out), .sel(t_ff_1_q));
  Multiplexer #(.select(5), .enable("false")) multiplexer_2 (
    .in0(Notes_Musique_1_1_b_1_out), .in1(Notes_Musique_1_1_b_2_out), .in2(Notes_Musique_1_1_e_1_out),
    .in3(Notes_Musique_1_1_e_2_out), .in4(Notes_Musique_1_1_e_3_out), .in5(Notes_Musique_1_1_g_1_out),
    .in6(Notes_Musique_1_1_f_1_out), .in7(Notes_Musique_1_1_f_2_out), .in8(Notes_Musique_1_1_e_4_out),
    .in9(Notes_Musique_1_1_e_5_out), .in10(Notes_Musique_1_1_e_6_out), .in11(Notes_Musique_1_1_e_7_out),
    .in12(Notes_Musique_1_1_b2_1_out), .in13(Notes_Musique_1_1_b2_2_out), .in14(Notes_Musique_1_1_a2_1_out),
    .in15(Notes_Musique_1_1_a2_2_out), .in16(Notes_Musique_1_1_a2_3_out), .in17(Notes_Musique_1_1_a2_4_out),
    .in18(Notes_Musique_1_1_a2_5_out), .in19(Notes_Musique_1_1_fs_1_out), .in20(Notes_Musique_1_1_fs_2_out),
    .in21(Notes_Musique_1_1_fs_3_out), .in22(Notes_Musique_1_1_fs_4_out), .in23(Notes_Musique_1_1_fs_5_out),
    .in24(Notes_Musique_1_1_e_8_out), .in25(Notes_Musique_1_1_e_9_out), .in26(Notes_Musique_1_1_e_10_out),
    .in27(Notes_Musique_1_1_g_2_out), .in28(Notes_Musique_1_1_f_3_out), .in29(Notes_Musique_1_1_f_4_out),
    .in30(Notes_Musique_1_1_ds_1_out), .in31(Notes_Musique_1_1_ds_2_out), .out(multiplexer_2_out),
    .sel(t_ff_5_q));
  and and_10 (and_10_out, multiplexer_2_out, ~or_2_out, and_1_out);  // AND_Gate
  and and_11 (and_11_out, multiplexer_1_out, ~or_1_out, and_2_out);  // AND_Gate
  or or_4 (Musique, and_10_out, and_11_out);

  assign Terre = 1'b0;
endmodule

module Stopwatch (
  input  [1:0] Stopwatch_in,
  output [29:0] Stopwatch_out
);

  wire clock_1_out, clock_2_out, nand_1_out, nand_2_out, nand_3_out, nand_4_out, nand_5_out, nand_6_out,
       nand_7_out, nand_8_out, nand_9_out, nand_10_out, nand_11_out, nand_12_out, nand_13_out, nand_14_out,
       or_1_out, or_2_out, s_r_ff_1_q, s_r_ff_2_q;

  nand nand_1 (nand_1_out, s_r_ff_1_q, s_r_ff_1_q);
  nand nand_2 (nand_2_out, s_r_ff_2_q, s_r_ff_2_q);
  nand nand_3 (nand_3_out, Stopwatch_in[0], s_r_ff_1_q, s_r_ff_2_q);
  nand nand_4 (nand_4_out, Stopwatch_in[0], Stopwatch_in[0]);
  nand nand_5 (nand_5_out, s_r_ff_2_q, s_r_ff_2_q);
  nand nand_6 (nand_6_out, Stopwatch_in[0], Stopwatch_in[0]);
  nand nand_7 (nand_7_out, s_r_ff_1_q, s_r_ff_1_q);
  nand nand_8 (nand_8_out, Stopwatch_in[0], nand_1_out, nand_2_out);
  nand nand_9 (nand_9_out, nand_3_out, nand_3_out);
  nand nand_10 (nand_10_out, nand_4_out, s_r_ff_1_q, nand_5_out);
  nand nand_11 (nand_11_out, nand_6_out, nand_7_out, s_r_ff_2_q);
  nand nand_12 (nand_12_out, nand_8_out, nand_8_out);
  nand nand_13 (nand_13_out, nand_10_out, nand_10_out);
  nand nand_14 (nand_14_out, nand_11_out, nand_11_out);
  S_R_Flip_Flop s_r_ff_1 (.clk(clock_1_out), .Q(s_r_ff_1_q), .reset(or_1_out), .preset(nand_12_out));  // open: S, R, Qn
  Clock clock_1 (.out(clock_1_out));
  or or_1 (or_1_out, nand_9_out, Stopwatch_in[1]);
  S_R_Flip_Flop s_r_ff_2 (.clk(clock_2_out), .Q(s_r_ff_2_q), .reset(or_2_out), .preset(nand_13_out));  // open: S, R, Qn
  Clock clock_2 (.out(clock_2_out));
  or or_2 (or_2_out, nand_14_out, Stopwatch_in[1]);
  Stopwatch_sous_circuit Stopwatch_sous_circuit_V5_1 (
    .enable(s_r_ff_1_q), .reset(Stopwatch_in[1]), .s1(Stopwatch_out[4:0]), .s2(Stopwatch_out[9:5]),
    .m1(Stopwatch_out[14:10]), .m2(Stopwatch_out[19:15]), .h1(Stopwatch_out[24:20]), .h2(Stopwatch_out[29:25]));

  // Notes on the sheet:
  //   Star_Stop_Stopwatch
  //   Reset_Stopwatch
  //   s1
  //   s2
  //   m1
  //   m2
  //   h1
  //   h2
endmodule

module Stopwatch_sous_circuit (
  input  enable,
  input  reset,
  output [4:0] s1,
  output [4:0] s2,
  output [4:0] m1,
  output [4:0] m2,
  output [4:0] h1,
  output [4:0] h2
);

  wire and_1_out, and_2_out, and_3_out, and_4_out, clock_1_out, counter_1_carry, counter_2_carry,
       counter_3_carry, counter_4_carry, counter_5_carry;

  Clock #(.highDuration(640), .lowDuration(640)) clock_1 (.out(clock_1_out));
  and and_1 (and_1_out, counter_1_carry, counter_2_carry);
  and and_2 (and_2_out, counter_1_carry, counter_2_carry, counter_3_carry);
  and and_3 (and_3_out, counter_1_carry, counter_2_carry, counter_3_carry, counter_4_carry);
  and and_4 (and_4_out, counter_1_carry, counter_2_carry, counter_3_carry, counter_4_carry, counter_5_carry);
  Counter #(.width(4), .max('h9)) counter_1 (
    .clr(reset), .load(1'b0), .up(1'b1), .count(enable), .clk(clock_1_out), .carry(counter_1_carry),
    .Q({s1[1], s1[2], s1[3], s1[4]}));  // open: D
  Counter #(.width(4), .max('h9)) counter_2 (
    .clr(reset), .load(1'b0), .up(1'b1), .count(counter_1_carry), .clk(clock_1_out), .carry(counter_2_carry),
    .Q({s2[1], s2[2], s2[3], s2[4]}));  // open: D
  Counter #(.width(4), .max('h9)) counter_3 (
    .clr(reset), .load(1'b0), .up(1'b1), .count(and_1_out), .clk(clock_1_out), .carry(counter_3_carry),
    .Q({m1[1], m1[2], m1[3], m1[4]}));  // open: D
  Counter #(.width(3), .max('h5)) counter_4 (
    .clr(reset), .load(1'b0), .up(1'b1), .count(and_2_out), .clk(clock_1_out), .carry(counter_4_carry),
    .Q({m2[2], m2[3], m2[4]}));  // open: D
  Counter #(.width(4), .max('h9)) counter_5 (
    .clr(reset), .load(1'b0), .up(1'b1), .count(and_3_out), .clk(clock_1_out), .carry(counter_5_carry),
    .Q({h1[1], h1[2], h1[3], h1[4]}));  // open: D
  Counter #(.width(3), .max('h5)) counter_6 (
    .clr(reset), .load(1'b0), .up(1'b1), .count(and_4_out), .clk(clock_1_out), .Q({h2[2], h2[3], h2[4]}));  // open: D, carry

  assign h1[0] = 1'b0;
  assign h2[1:0] = 2'b00;
  assign m1[0] = 1'b0;
  assign m2[1:0] = 2'b00;
  assign s1[0] = 1'b0;
  assign s2[0] = 1'b0;
endmodule

module Horloge (
  input  [8:0] Horloge_in,
  output [29:0] Horloge_out
);

  wire and_1_out, and_2_out, and_3_out, and_4_out, and_5_out, and_6_out, and_7_out,
       Detecteur_flanc_montant_1_sortie, nor_1_out, not_1_out;
  wire [4:0] Set_Digits_1_h1, Set_Digits_1_h2, Set_Digits_1_m1, Set_Digits_1_m2, Set_Digits_1_s1,
       Set_Digits_1_s2;

  Detecteur_flanc_montant Detecteur_flanc_montant_1 (.Entree(Horloge_in[1]), .Sortie(Detecteur_flanc_montant_1_sortie));
  and and_1 (and_1_out, Detecteur_flanc_montant_1_sortie, Horloge_in[0]);
  and and_2 (and_2_out, Horloge_in[2], Horloge_in[0]);
  and and_3 (and_3_out, Horloge_in[3], Horloge_in[0]);
  and and_4 (and_4_out, Horloge_in[4], Horloge_in[0]);
  and and_5 (and_5_out, Horloge_in[5], Horloge_in[0]);
  and and_6 (and_6_out, Horloge_in[6], Horloge_in[0]);
  and and_7 (and_7_out, Horloge_in[7], Horloge_in[0]);
  nor nor_1 (nor_1_out, Horloge_in[7], Horloge_in[6], Horloge_in[5], Horloge_in[4], Horloge_in[3], Horloge_in[2]);
  Set_Digits Set_Digits_1 (
    .activation(Horloge_in[0]), .Set_digit(and_1_out), .s1_in(and_2_out), .s2_in(and_3_out),
    .m1_in(and_4_out), .m2_in(and_5_out), .h1_in(and_6_out), .h2_in(and_7_out), .reset_digit(Horloge_in[8]),
    .s1(Set_Digits_1_s1), .s2(Set_Digits_1_s2), .m1(Set_Digits_1_m1), .m2(Set_Digits_1_m2),
    .h1(Set_Digits_1_h1), .h2(Set_Digits_1_h2));
  not not_1 (not_1_out, nor_1_out);
  Horloge_fonctionnement Horloge_fonctionnement_1 (
    .stop_set(not_1_out), .enable(nor_1_out), .reset(Horloge_in[8]), .set_s1(Set_Digits_1_s1),
    .set_s2(Set_Digits_1_s2), .set_m1(Set_Digits_1_m1), .set_m2(Set_Digits_1_m2), .set_h1(Set_Digits_1_h1),
    .set_h2(Set_Digits_1_h2), .Output_bus_1(Horloge_out[4:0]), .Output_bus_2(Horloge_out[9:5]),
    .Output_bus_3(Horloge_out[14:10]), .Output_bus_4(Horloge_out[19:15]), .Output_bus_5(Horloge_out[24:20]),
    .Output_bus_6(Horloge_out[29:25]));

  // Notes on the sheet:
  //   Horloge_mode
  //   Bouton
  //   set_s1_Horloge
  //   set_s2_Horloge
  //   set_m1_Horloge
  //   set_m2_Horloge
  //   set_h1_Horloge
  //   set_h2_Horloge
  //   reset_Horloge
  //   s1
  //   s2
  //   m1
  //   m2
  //   h1
  //   h2
endmodule

module Horloge_fonctionnement (
  input  stop_set,
  input  enable,
  input  reset,
  input  [4:0] set_s1,
  input  [4:0] set_s2,
  input  [4:0] set_m1,
  input  [4:0] set_m2,
  input  [4:0] set_h1,
  input  [4:0] set_h2,
  output [4:0] Output_bus_1,
  output [4:0] Output_bus_2,
  output [4:0] Output_bus_3,
  output [4:0] Output_bus_4,
  output [4:0] Output_bus_5,
  output [4:0] Output_bus_6
);

  wire and_1_out, and_2_out, and_3_out, and_4_out, and_5_out, and_6_out, and_7_out, clock_1_out,
       counter_1_carry, counter_2_carry, counter_3_carry, counter_4_carry, counter_5_carry, counter_6_carry,
       counter_7_carry, nand_1_out, nand_2_out, nand_3_out, or_1_out, or_2_out, or_3_out;

  Clock #(.highDuration(640), .lowDuration(640)) clock_1 (.out(clock_1_out));
  and and_1 (and_1_out, counter_1_carry, enable);
  and and_2 (and_2_out, counter_2_carry, counter_1_carry, enable);
  and and_3 (and_3_out, counter_1_carry, counter_2_carry, enable, counter_3_carry);
  and and_4 (and_4_out, counter_1_carry, counter_3_carry, counter_2_carry, counter_4_carry, enable);
  and and_5 (and_5_out, counter_1_carry, counter_4_carry, counter_3_carry, counter_5_carry, counter_2_carry, enable);
  and and_6 (and_6_out, counter_1_carry, counter_3_carry, counter_4_carry, counter_2_carry, counter_5_carry, counter_6_carry, enable);
  and and_7 (and_7_out, counter_5_carry, counter_1_carry, counter_3_carry, counter_4_carry, counter_6_carry, or_3_out, counter_2_carry, enable);
  Counter #(.width(4), .max('h9)) counter_1 (
    .clr(reset), .load(stop_set), .up(1'b1), .count(enable), .clk(clock_1_out), .carry(counter_1_carry));  // open: D, Q
  Counter #(.width(4), .max('h9)) counter_2 (
    .clr(reset), .load(stop_set), .up(1'b1), .count(and_1_out), .clk(clock_1_out), .carry(counter_2_carry));  // open: D, Q
  Counter #(.width(4), .max('h9)) counter_3 (
    .clr(reset), .load(stop_set), .up(1'b1), .count(and_2_out), .clk(clock_1_out),
    .D({set_s1[1], set_s1[2], set_s1[3], set_s1[4]}), .carry(counter_3_carry),
    .Q({Output_bus_1[1], Output_bus_1[2], Output_bus_1[3], Output_bus_1[4]}));
  Counter #(.width(3), .max('h5)) counter_4 (
    .clr(reset), .load(stop_set), .up(1'b1), .count(and_3_out), .clk(clock_1_out),
    .D({set_s2[2], set_s2[3], set_s2[4]}), .carry(counter_4_carry),
    .Q({Output_bus_2[2], Output_bus_2[3], Output_bus_2[4]}));
  Counter #(.width(4), .max('h9)) counter_5 (
    .clr(reset), .load(stop_set), .up(1'b1), .count(and_4_out), .clk(clock_1_out),
    .D({set_m1[1], set_m1[2], set_m1[3], set_m1[4]}), .carry(counter_5_carry),
    .Q({Output_bus_3[1], Output_bus_3[2], Output_bus_3[3], Output_bus_3[4]}));
  Counter #(.width(3), .max('h5)) counter_6 (
    .clr(reset), .load(stop_set), .up(1'b1), .count(and_5_out), .clk(clock_1_out),
    .D({set_m2[2], set_m2[3], set_m2[4]}), .carry(counter_6_carry),
    .Q({Output_bus_4[2], Output_bus_4[3], Output_bus_4[4]}));
  Counter #(.width(4), .max('h9)) counter_7 (
    .clr(or_1_out), .load(stop_set), .up(1'b1), .count(and_6_out), .clk(clock_1_out),
    .D({set_h1[1], set_h1[2], set_h1[3], set_h1[4]}), .carry(counter_7_carry),
    .Q({Output_bus_5[1], Output_bus_5[2], Output_bus_5[3], Output_bus_5[4]}));
  or or_1 (or_1_out, reset, nand_3_out);
  Counter #(.width(2), .max('h2)) counter_8 (
    .clr(or_2_out), .load(stop_set), .up(1'b1), .count(and_7_out), .clk(clock_1_out),
    .D({set_h2[3], set_h2[4]}), .Q({Output_bus_6[3], Output_bus_6[4]}));  // open: carry
  or or_2 (or_2_out, reset, nand_3_out);
  or or_3 (or_3_out, counter_7_carry, nand_3_out);
  nand nand_1 (nand_1_out, Output_bus_6[3], Output_bus_5[1]);
  nand nand_2 (nand_2_out, Output_bus_6[3], Output_bus_5[2]);
  nand nand_3 (nand_3_out, nand_1_out, nand_2_out);

  assign Output_bus_1[0] = set_s1[0];
  assign Output_bus_2[1:0] = {1'b0, set_s2[0]};
  assign Output_bus_3[0] = set_m1[0];
  assign Output_bus_4[1:0] = {1'b0, set_m2[0]};
  assign Output_bus_5[0] = set_h1[0];
  assign Output_bus_6[2:0] = {2'b00, set_h2[0]};
endmodule
module Timer (
  input  [8:0] Timer_in,
  output [29:0] Timer_out,
  output Zero
);

  wire and_1_out, and_2_out, and_3_out, and_4_out, and_5_out, and_6_out, and_7_out, and_8_out, clock_1_out,
       demultiplexer_1_out0, demultiplexer_1_out1, Detecteur_flanc_montant_1_sortie, nand_1_out, nand_2_out,
       nand_3_out, nand_4_out, nand_5_out, nand_6_out, nand_7_out, nand_8_out, nand_9_out, nand_10_out,
       nand_11_out, nand_12_out, nand_13_out, nand_14_out, not_1_out, or_1_out, or_2_out, or_3_out, or_4_out,
       s_r_ff_1_q, s_r_ff_2_q, s_r_ff_3_q, Timer_fonctionnement_1_output_1;
  wire [4:0] Set_Digits_1_h1, Set_Digits_1_h2, Set_Digits_1_m1, Set_Digits_1_m2, Set_Digits_1_s1,
       Set_Digits_1_s2;

  Detecteur_flanc_montant Detecteur_flanc_montant_1 (.Entree(Timer_in[1]), .Sortie(Detecteur_flanc_montant_1_sortie));
  Demultiplexer #(.enable("false")) demultiplexer_1 (
    .out0(demultiplexer_1_out0), .out1(demultiplexer_1_out1), .in(Detecteur_flanc_montant_1_sortie),
    .sel(or_1_out));
  or or_1 (or_1_out, Timer_in[2], Timer_in[3], Timer_in[4], Timer_in[5], Timer_in[6], Timer_in[7]);
  and and_1 (and_1_out, demultiplexer_1_out1, Timer_in[0]);
  and and_2 (and_2_out, Timer_in[2], not_1_out, Timer_in[0]);
  and and_3 (and_3_out, Timer_in[3], not_1_out, Timer_in[0]);
  and and_4 (and_4_out, Timer_in[4], not_1_out, Timer_in[0]);
  and and_5 (and_5_out, Timer_in[5], not_1_out, Timer_in[0]);
  and and_6 (and_6_out, Timer_in[6], not_1_out, Timer_in[0]);
  and and_7 (and_7_out, Timer_in[7], not_1_out, Timer_in[0]);
  and and_8 (and_8_out, Timer_in[0], demultiplexer_1_out0);
  nand nand_1 (nand_1_out, s_r_ff_2_q, s_r_ff_2_q);
  nand nand_2 (nand_2_out, s_r_ff_1_q, s_r_ff_1_q);
  nand nand_3 (nand_3_out, and_8_out, s_r_ff_2_q, s_r_ff_1_q);
  nand nand_4 (nand_4_out, and_8_out, and_8_out);
  nand nand_5 (nand_5_out, s_r_ff_1_q, s_r_ff_1_q);
  nand nand_6 (nand_6_out, and_8_out, and_8_out);
  nand nand_7 (nand_7_out, s_r_ff_2_q, s_r_ff_2_q);
  not not_1 (not_1_out, s_r_ff_2_q);
  nand nand_8 (nand_8_out, and_8_out, nand_1_out, nand_2_out);
  nand nand_9 (nand_9_out, nand_3_out, nand_3_out);
  nand nand_10 (nand_10_out, nand_4_out, s_r_ff_2_q, nand_5_out);
  nand nand_11 (nand_11_out, nand_6_out, nand_7_out, s_r_ff_1_q);
  nand nand_12 (nand_12_out, nand_8_out, nand_8_out);
  nand nand_13 (nand_13_out, nand_10_out, nand_10_out);
  nand nand_14 (nand_14_out, nand_11_out, nand_11_out);
  or or_2 (or_2_out, Timer_fonctionnement_1_output_1, or_1_out, nand_9_out, Timer_in[8]);
  S_R_Flip_Flop s_r_ff_1 (.clk(clock_1_out), .Q(s_r_ff_1_q), .reset(or_3_out), .preset(nand_13_out));  // open: S, R, Qn
  Clock clock_1 (.out(clock_1_out));
  S_R_Flip_Flop s_r_ff_2 (.clk(clock_1_out), .Q(s_r_ff_2_q), .reset(or_2_out), .preset(nand_12_out));  // open: S, R, Qn
  or or_3 (or_3_out, or_1_out, nand_14_out, Timer_in[8], Timer_fonctionnement_1_output_1);
  Set_Digits Set_Digits_1 (
    .activation(Timer_in[0]), .Set_digit(and_1_out), .s1_in(and_2_out), .s2_in(and_3_out), .m1_in(and_4_out),
    .m2_in(and_5_out), .h1_in(and_6_out), .h2_in(and_7_out), .reset_digit(Timer_in[8]), .s1(Set_Digits_1_s1),
    .s2(Set_Digits_1_s2), .m1(Set_Digits_1_m1), .m2(Set_Digits_1_m2), .h1(Set_Digits_1_h1),
    .h2(Set_Digits_1_h2));
  or or_4 (or_4_out, or_1_out, Timer_fonctionnement_1_output_1);
  S_R_Flip_Flop s_r_ff_3 (.Q(s_r_ff_3_q), .reset(Timer_in[8]), .preset(s_r_ff_2_q));  // open: S, R, clk, Qn
  Timer_fonctionnement Timer_fonctionnement_1 (
    .set_s1(Set_Digits_1_s1), .set_s2(Set_Digits_1_s2), .set_m1(Set_Digits_1_m1), .set_m2(Set_Digits_1_m2),
    .set_h1(Set_Digits_1_h1), .set_h2(Set_Digits_1_h2), .stop_set(or_4_out), .enable(s_r_ff_2_q),
    .reset(Timer_in[8]), .Output_bus_1(Timer_out[4:0]), .Output_bus_2(Timer_out[9:5]),
    .Output_bus_3(Timer_out[14:10]), .Output_bus_4(Timer_out[19:15]), .Output_bus_5(Timer_out[24:20]),
    .Output_bus_6(Timer_out[29:25]), .Output_1(Timer_fonctionnement_1_output_1));
  and and_9 (Zero, Timer_fonctionnement_1_output_1, s_r_ff_3_q);

  // Notes on the sheet:
  //   Mode_Timer
  //   Bouton_Action_Timer
  //   set_s1_Timer
  //   set_s2_Timer
  //   set_m1_Timer
  //   set_m2_Timer
  //   set_h1_Timer
  //   set_h2_Timer
  //   reset_Timer
  //   Set_Digit
  //   Start_Stop
  //   s1
  //   s2
  //   m1
  //   m2
  //   h1
  //   h2
endmodule

module Timer_fonctionnement (
  input  [4:0] set_s1,
  input  [4:0] set_s2,
  input  [4:0] set_m1,
  input  [4:0] set_m2,
  input  [4:0] set_h1,
  input  [4:0] set_h2,
  input  stop_set,
  input  enable,
  input  reset,
  output [4:0] Output_bus_1,
  output [4:0] Output_bus_2,
  output [4:0] Output_bus_3,
  output [4:0] Output_bus_4,
  output [4:0] Output_bus_5,
  output [4:0] Output_bus_6,
  output Output_1
);

  wire and_1_out, and_2_out, and_3_out, and_4_out, and_5_out, and_6_out, and_7_out, and_8_out, and_9_out,
       and_10_out, and_11_out, and_12_out, and_13_out, clock_1_out, counter_1_carry, counter_2_carry,
       counter_3_carry, counter_4_carry, counter_5_carry, counter_6_carry, counter_7_carry;

  Clock #(.highDuration(640), .lowDuration(640)) clock_1 (.out(clock_1_out));
  and and_1 (and_1_out, counter_1_carry, enable);
  and and_2 (and_2_out, counter_1_carry, enable, counter_2_carry);
  and and_3 (and_3_out, counter_1_carry, enable, counter_3_carry, counter_2_carry);
  and and_4 (and_4_out, counter_1_carry, counter_4_carry, enable, counter_3_carry, counter_2_carry);
  and and_5 (and_5_out, counter_1_carry, enable, counter_5_carry, counter_4_carry, counter_3_carry, counter_2_carry);
  and and_6 (and_6_out, counter_1_carry, counter_6_carry, counter_5_carry, enable, counter_4_carry, counter_3_carry, counter_2_carry);
  and and_7 (and_7_out, counter_1_carry, enable, counter_7_carry, counter_6_carry, counter_5_carry, counter_4_carry, counter_3_carry, counter_2_carry);
  Counter #(.width(4), .max('h9)) counter_1 (
    .clr(reset), .load(stop_set), .up(1'b0), .count(enable), .clk(clock_1_out), .D(4'b0000),
    .carry(counter_1_carry));  // open: Q
  Counter #(.width(4), .max('h9)) counter_2 (
    .clr(reset), .load(stop_set), .up(1'b0), .count(and_1_out), .clk(clock_1_out), .D(4'b0000),
    .carry(counter_2_carry));  // open: Q
  Counter #(.width(4), .max('h9)) counter_3 (
    .clr(reset), .load(stop_set), .up(1'b0), .count(and_2_out), .clk(clock_1_out),
    .D({set_s1[1], set_s1[2], set_s1[3], set_s1[4]}), .carry(counter_3_carry),
    .Q({Output_bus_1[1], Output_bus_1[2], Output_bus_1[3], Output_bus_1[4]}));
  Counter #(.width(3), .max('h5)) counter_4 (
    .clr(reset), .load(stop_set), .up(1'b0), .count(and_3_out), .clk(clock_1_out),
    .D({set_s2[2], set_s2[3], set_s2[4]}), .carry(counter_4_carry),
    .Q({Output_bus_2[2], Output_bus_2[3], Output_bus_2[4]}));
  Counter #(.width(4), .max('h9)) counter_5 (
    .clr(reset), .load(stop_set), .up(1'b0), .count(and_4_out), .clk(clock_1_out),
    .D({set_m1[1], set_m1[2], set_m1[3], set_m1[4]}), .carry(counter_5_carry),
    .Q({Output_bus_3[1], Output_bus_3[2], Output_bus_3[3], Output_bus_3[4]}));
  Counter #(.width(3), .max('h5)) counter_6 (
    .clr(reset), .load(stop_set), .up(1'b0), .count(and_5_out), .clk(clock_1_out),
    .D({set_m2[2], set_m2[3], set_m2[4]}), .carry(counter_6_carry),
    .Q({Output_bus_4[2], Output_bus_4[3], Output_bus_4[4]}));
  Counter #(.width(4), .max('h9)) counter_7 (
    .clr(reset), .load(stop_set), .up(1'b0), .count(and_6_out), .clk(clock_1_out),
    .D({set_h1[1], set_h1[2], set_h1[3], set_h1[4]}), .carry(counter_7_carry),
    .Q({Output_bus_5[1], Output_bus_5[2], Output_bus_5[3], Output_bus_5[4]}));
  Counter #(.width(2), .max('h2)) counter_8 (
    .clr(reset), .load(stop_set), .up(1'b0), .count(and_7_out), .clk(clock_1_out),
    .D({set_h2[3], set_h2[4]}), .Q({Output_bus_6[3], Output_bus_6[4]}));  // open: carry
  and and_8 (and_8_out, ~Output_bus_6[3], ~Output_bus_6[4]);  // AND_Gate
  and and_9 (and_9_out, ~Output_bus_1[1], ~Output_bus_1[2], ~Output_bus_1[3], ~Output_bus_1[4]);  // AND_Gate
  and and_10 (and_10_out, ~Output_bus_2[2], ~Output_bus_2[3], ~Output_bus_2[4]);  // AND_Gate
  and and_11 (and_11_out, ~Output_bus_3[1], ~Output_bus_3[2], ~Output_bus_3[3], ~Output_bus_3[4]);  // AND_Gate
  and and_12 (and_12_out, ~Output_bus_4[2], ~Output_bus_4[3], ~Output_bus_4[4]);  // AND_Gate
  and and_13 (and_13_out, ~Output_bus_5[1], ~Output_bus_5[2], ~Output_bus_5[3], ~Output_bus_5[4]);  // AND_Gate
  and and_14 (Output_1, and_9_out, and_10_out, and_11_out, and_12_out, and_13_out, and_8_out);

  assign Output_bus_1[0] = set_s1[0];
  assign Output_bus_2[1:0] = {1'b0, set_s2[0]};
  assign Output_bus_3[0] = set_m1[0];
  assign Output_bus_4[1:0] = {1'b0, set_m2[0]};
  assign Output_bus_5[0] = set_h1[0];
  assign Output_bus_6[2:0] = {2'b00, set_h2[0]};
endmodule

module Reset_Manager (
  input  Reset_Horloge_in,
  input  Reset_Alarm_in,
  input  Reset_Fuseaux_horaires_in,
  input  Reset_Stopwatch_in,
  input  Reset_Timer_in,
  input  Reset_all,
  output Reset_Horloge,
  output Reset_Alarm,
  output Reset_Fuseaux_horaires,
  output Reset_Stopwatch,
  output Reset_Timer
);

  or or_1 (Reset_Horloge, Reset_Horloge_in, Reset_all);
  or or_2 (Reset_Alarm, Reset_Alarm_in, Reset_all);
  or or_3 (Reset_Fuseaux_horaires, Reset_Fuseaux_horaires_in, Reset_all);
  or or_4 (Reset_Stopwatch, Reset_Stopwatch_in, Reset_all);
  or or_5 (Reset_Timer, Reset_Timer_in, Reset_all);
endmodule

module Demux_Manager (
  input  [2:0] Mode,
  input  Bouton_action,
  input  Stand_by_Alarm_in,
  input  s1_in,
  input  s2_in,
  input  m1_in,
  input  m2_in,
  input  h1_in,
  input  h2_in,
  input  Reset_All,
  input  Musique_on,
  output LED_Horloge,
  output [8:0] Horloge,
  output LED_Alarm,
  output [9:0] Alarm,
  output LED_Stopwatch,
  output [1:0] Stopwatch,
  output LED_Timer,
  output [8:0] Timer,
  output LED_Fuseau_horaire,
  output [2:0] Fuseau_horaire,
  output Stop_musique
);

  wire and_1_out, clock_1_out, d_ff_1_q, d_ff_1_qn, demultiplexer_1_out0, demultiplexer_11_out0,
       demultiplexer_11_out1, demultiplexer_11_out2, demultiplexer_11_out3, demultiplexer_11_out4,
       Detecteur_flanc_montant_2_1_sortie, Detecteur_reset_1_reset, or_1_out, s_r_ff_1_q;

  Detecteur_flanc_montant_reset Detecteur_flanc_montant_2_1 (
    .Entree(Bouton_action), .Sortie(Detecteur_flanc_montant_2_1_sortie));
  D_Flip_Flop d_ff_1 (
    .D(and_1_out), .clk(clock_1_out), .Q(d_ff_1_q), .Qn(d_ff_1_qn), .reset(Reset_All));  // open: preset
  and and_1 (and_1_out, d_ff_1_qn, Detecteur_flanc_montant_2_1_sortie);
  Clock #(.highDuration(10000), .lowDuration(10000)) clock_1 (.out(clock_1_out));
  S_R_Flip_Flop s_r_ff_1 (.Q(s_r_ff_1_q), .reset(or_1_out), .preset(Musique_on));  // open: S, R, clk, Qn
  Demultiplexer #(.enable("false")) demultiplexer_1 (
    .out0(demultiplexer_1_out0), .out1(Stop_musique), .in(Bouton_action), .sel(s_r_ff_1_q));
  Detecteur_reset Detecteur_reset_1 (.Bouton(Bouton_action), .Reset(Detecteur_reset_1_reset));
  or or_1 (or_1_out, d_ff_1_q, Reset_All);
  Demultiplexer #(.select(3), .enable("false")) demultiplexer_2 (
    .out0(Horloge[0]), .out1(Alarm[1]), .out2(Fuseau_horaire[1]), .out3(LED_Stopwatch), .out4(LED_Timer),
    .in(1'b1), .sel(Mode));  // open: out5, out6, out7
  Demultiplexer #(.select(3), .enable("false")) demultiplexer_3 (
    .out0(Horloge[1]), .out1(Alarm[2]), .out2(Fuseau_horaire[2]), .out3(Stopwatch[0]), .out4(Timer[1]),
    .in(demultiplexer_1_out0), .sel(Mode));  // open: out5, out6, out7
  Demultiplexer #(.select(3), .enable("false")) demultiplexer_4 (
    .out1(Alarm[0]), .in(Stand_by_Alarm_in), .sel(Mode));  // open: out0, out2, out3, out4, out5, out6, out7
  Demultiplexer #(.select(3), .enable("false")) demultiplexer_5 (
    .out0(Horloge[2]), .out1(Alarm[3]), .out4(Timer[2]), .in(s1_in), .sel(Mode));  // open: out2, out3, out5, out6, out7
  Demultiplexer #(.select(3), .enable("false")) demultiplexer_6 (
    .out0(Horloge[3]), .out1(Alarm[4]), .out4(Timer[3]), .in(s2_in), .sel(Mode));  // open: out2, out3, out5, out6, out7
  Demultiplexer #(.select(3), .enable("false")) demultiplexer_7 (
    .out0(Horloge[4]), .out1(Alarm[5]), .out4(Timer[4]), .in(m1_in), .sel(Mode));  // open: out2, out3, out5, out6, out7
  Demultiplexer #(.select(3), .enable("false")) demultiplexer_8 (
    .out0(Horloge[5]), .out1(Alarm[6]), .out4(Timer[5]), .in(m2_in), .sel(Mode));  // open: out2, out3, out5, out6, out7
  Demultiplexer #(.select(3), .enable("false")) demultiplexer_9 (
    .out0(Horloge[6]), .out1(Alarm[7]), .out4(Timer[6]), .in(h1_in), .sel(Mode));  // open: out2, out3, out5, out6, out7
  Demultiplexer #(.select(3), .enable("false")) demultiplexer_10 (
    .out0(Horloge[7]), .out1(Alarm[8]), .out4(Timer[7]), .in(h2_in), .sel(Mode));  // open: out2, out3, out5, out6, out7
  Demultiplexer #(.select(3), .enable("false")) demultiplexer_11 (
    .out0(demultiplexer_11_out0), .out1(demultiplexer_11_out1), .out2(demultiplexer_11_out2),
    .out3(demultiplexer_11_out3), .out4(demultiplexer_11_out4), .in(Detecteur_reset_1_reset), .sel(Mode));  // open: out5, out6, out7
  Reset_Manager Reset_Manager_1 (
    .Reset_Horloge_in(demultiplexer_11_out0), .Reset_Alarm_in(demultiplexer_11_out1),
    .Reset_Fuseaux_horaires_in(demultiplexer_11_out2), .Reset_Stopwatch_in(demultiplexer_11_out3),
    .Reset_Timer_in(demultiplexer_11_out4), .Reset_all(Reset_All), .Reset_Horloge(Horloge[8]),
    .Reset_Alarm(Alarm[9]), .Reset_Fuseaux_horaires(Fuseau_horaire[0]), .Reset_Stopwatch(Stopwatch[1]),
    .Reset_Timer(Timer[8]));

  assign LED_Alarm = Alarm[1];
  assign LED_Fuseau_horaire = Fuseau_horaire[1];
  assign LED_Horloge = Horloge[0];
  assign Timer[0] = LED_Timer;

  // Notes on the sheet:
  //   Horloge_mode
  //   Bouton
  //   set_s1_Horloge
  //   set_s2_Horloge
  //   set_m1_Horloge
  //   set_m2_Horloge
  //   set_h1_Horloge
  //   set_h2_Horloge
  //   reset_Horloge
  //   Mode_Timer
  //   set_s1_Timer
  //   set_s2_Timer
  //   set_m1_Timer
  //   set_m2_Timer
  //   set_h1_Timer
  //   set_h2_Timer
  //   reset_Timer
  //   Reset_Fuseau_horaire
  //   Activation_Fuseau_horaire
  //   Bouton_Action_Fuseau_horaire
  //   Stand_by_Alarm
  //   mode_Alarm
  //   Set_digit_Alarm
  //   set_s1_Alarm
  //   set_s2_Alarm
  //   set_m1_Alarm
  //   set_m2_Alarm
  //   set_h1_Alarm
  //   set_h2_Alarm
  //   reset_Alarm
  //   Star_Stop_Stopwatch
  //   Reset_Stopwatch
  //   Bouton_Action_Timer
endmodule

module Mux_Manager (
  input  [2:0] Mode,
  input  [29:0] Horloge,
  input  [29:0] Alarm,
  input  [29:0] Stopwatch,
  input  [29:0] Timer,
  output [29:0] Mux_out
);

  Multiplexer #(.select(3), .width(5), .enable("false")) multiplexer_1 (
    .in0(Horloge[4:0]), .in1(Alarm[4:0]), .in2(Horloge[4:0]), .in3(Stopwatch[4:0]), .in4(Timer[4:0]),
    .out(Mux_out[4:0]), .sel(Mode));  // open: in5, in6, in7
  Multiplexer #(.select(3), .width(5), .enable("false")) multiplexer_2 (
    .in0(Horloge[9:5]), .in1(Alarm[9:5]), .in2(Horloge[9:5]), .in3(Stopwatch[9:5]), .in4(Timer[9:5]),
    .out(Mux_out[9:5]), .sel(Mode));  // open: in5, in6, in7
  Multiplexer #(.select(3), .width(5), .enable("false")) multiplexer_3 (
    .in0(Horloge[14:10]), .in1(Alarm[14:10]), .in2(Horloge[14:10]), .in3(Stopwatch[14:10]),
    .in4(Timer[14:10]), .out(Mux_out[14:10]), .sel(Mode));  // open: in5, in6, in7
  Multiplexer #(.select(3), .width(5), .enable("false")) multiplexer_4 (
    .in0(Horloge[19:15]), .in1(Alarm[19:15]), .in2(Horloge[19:15]), .in3(Stopwatch[19:15]),
    .in4(Timer[19:15]), .out(Mux_out[19:15]), .sel(Mode));  // open: in5, in6, in7
  Multiplexer #(.select(3), .width(5), .enable("false")) multiplexer_5 (
    .in0(Horloge[24:20]), .in1(Alarm[24:20]), .in2(Horloge[24:20]), .in3(Stopwatch[24:20]),
    .in4(Timer[24:20]), .out(Mux_out[24:20]), .sel(Mode));  // open: in5, in6, in7
  Multiplexer #(.select(3), .width(5), .enable("false")) multiplexer_6 (
    .in0(Horloge[29:25]), .in1(Alarm[29:25]), .in2(Horloge[29:25]), .in3(Stopwatch[29:25]),
    .in4(Timer[29:25]), .out(Mux_out[29:25]), .sel(Mode));  // open: in5, in6, in7

  // Notes on the sheet:
  //   m2_Alarm
  //   s1_Horloge
  //   s2_Horloge
  //   m1_Horloge
  //   m2_Horloge
  //   h1_Horloge
  //   h2_Horloge
  //   s1_Alarm
  //   s2_Alarm
  //   m1_Alarm
  //   h1_Alarm
  //   h2_Alarm
  //   s1_Stopwatch
  //   s2_Stopwatch
  //   m1_Stopwatch
  //   m2_Stopwatch
  //   h1_Stopwatch
  //   h2_Stopwatch
  //   s1_Timer
  //   s2_Timer
  //   m1_Timer
  //   m2_Timer
  //   h1_Timer
  //   h2_Timer
  //   s1
  //   s2
  //   m1
  //   m2
  //   h1
  //   h2
endmodule

module Detecteur_flanc_montant_reset (
  input  Entree,
  output Sortie
);

  wire clock_1_out, d_ff_1_q, d_ff_2_q, d_ff_3_q;

  Clock #(.highDuration(6000), .lowDuration(60000)) clock_1 (.out(clock_1_out));
  D_Flip_Flop d_ff_1 (.D(Entree), .clk(clock_1_out), .Q(d_ff_1_q));  // open: Qn, preset, reset
  D_Flip_Flop d_ff_2 (.D(d_ff_1_q), .clk(clock_1_out), .Q(d_ff_2_q));  // open: Qn, preset, reset
  D_Flip_Flop d_ff_3 (.D(d_ff_2_q), .clk(clock_1_out), .Q(d_ff_3_q));  // open: Qn, preset, reset
  and and_1 (Sortie, d_ff_1_q, d_ff_2_q, ~d_ff_3_q);  // AND_Gate
endmodule

module Detecteur_flanc_montant (
  input  Entree,
  output Sortie
);

  wire clock_1_out, d_ff_1_q, d_ff_2_q, d_ff_3_q;

  Clock #(.highDuration(640), .lowDuration(640)) clock_1 (.out(clock_1_out));
  D_Flip_Flop d_ff_1 (.D(Entree), .clk(clock_1_out), .Q(d_ff_1_q));  // open: Qn, preset, reset
  D_Flip_Flop d_ff_2 (.D(d_ff_1_q), .clk(clock_1_out), .Q(d_ff_2_q));  // open: Qn, preset, reset
  D_Flip_Flop d_ff_3 (.D(d_ff_2_q), .clk(clock_1_out), .Q(d_ff_3_q));  // open: Qn, preset, reset
  and and_1 (Sortie, d_ff_1_q, d_ff_2_q, ~d_ff_3_q);  // AND_Gate
endmodule

module Detecteur_reset (
  input  Bouton,
  output Reset
);

  wire and_1_out, and_2_out, and_3_out, and_4_out, clock_1_out, not_1_out, t_ff_1_q, t_ff_2_q, t_ff_3_q,
       t_ff_4_q, t_ff_5_q;

  Clock #(.highDuration(7000), .lowDuration(7000)) clock_1 (.out(clock_1_out));
  not not_1 (not_1_out, Bouton);
  T_Flip_Flop t_ff_1 (.T(Bouton), .clk(clock_1_out), .Q(t_ff_1_q), .reset(not_1_out));  // open: Qn, preset
  T_Flip_Flop t_ff_2 (.T(and_1_out), .clk(clock_1_out), .Q(t_ff_2_q), .reset(not_1_out));  // open: Qn, preset
  and and_1 (and_1_out, t_ff_1_q, Bouton);
  T_Flip_Flop t_ff_3 (.T(and_2_out), .clk(clock_1_out), .Q(t_ff_3_q), .reset(not_1_out));  // open: Qn, preset
  and and_2 (and_2_out, t_ff_2_q, t_ff_1_q, Bouton);
  T_Flip_Flop t_ff_4 (.T(and_3_out), .clk(clock_1_out), .Q(t_ff_4_q), .reset(not_1_out));  // open: Qn, preset
  and and_3 (and_3_out, t_ff_3_q, t_ff_2_q, t_ff_1_q, Bouton);
  T_Flip_Flop t_ff_5 (.T(and_4_out), .clk(clock_1_out), .Q(t_ff_5_q), .reset(not_1_out));  // open: Qn, preset
  and and_4 (and_4_out, t_ff_4_q, t_ff_3_q, t_ff_2_q, t_ff_1_q, Bouton);
  S_R_Flip_Flop s_r_ff_1 (.Q(Reset), .reset(not_1_out), .preset(t_ff_5_q));  // open: S, R, clk, Qn
endmodule
